// Logisim project gpu32.circ as structural Verilog: 27 circuits, main circuit main
module main (
  input  [6:0] FB_Addr_Page,
  input  in_2,
  input  in_3,
  input  [11:0] in_4,
  input  [31:0] in_5
);

  wire clock_1_out, clock_2_out, g32_1_ram_stb, g32_1_ram_wr, memory_be_1_ram_ack, not_1_out, Reset_out;
  wire [3:0] g32_1_ram_be;
  wire [6:0] framebuffer_1_fb_addr_page_2, framebuffer_2_fb_addr_page_2, framebuffer_4_fb_addr_page_2;
  wire [15:0] g32_1_ram_addr, g32_1_rom_addr;
  wire [31:0] framebuffer_1_col0, framebuffer_1_col0_2, framebuffer_1_col0_3, framebuffer_1_col0_4,
       framebuffer_1_col1, framebuffer_1_col1_2, framebuffer_1_col1_3, framebuffer_1_col1_4,
       framebuffer_1_col2, framebuffer_1_col2_2, framebuffer_1_col2_3, framebuffer_1_col2_4,
       framebuffer_1_col3, framebuffer_1_col3_2, framebuffer_1_col3_3, framebuffer_1_col3_4,
       framebuffer_1_col4, framebuffer_1_col4_2, framebuffer_1_col4_3, framebuffer_1_col4_4,
       framebuffer_1_col5, framebuffer_1_col5_2, framebuffer_1_col5_3, framebuffer_1_col5_4,
       framebuffer_1_col6, framebuffer_1_col6_2, framebuffer_1_col6_3, framebuffer_1_col6_4,
       framebuffer_1_col7, framebuffer_1_col7_2, framebuffer_1_col7_3, framebuffer_1_col7_4,
       framebuffer_2_col0, framebuffer_2_col0_2, framebuffer_2_col0_3, framebuffer_2_col0_4,
       framebuffer_2_col1, framebuffer_2_col1_2, framebuffer_2_col1_3, framebuffer_2_col1_4,
       framebuffer_2_col2, framebuffer_2_col2_2, framebuffer_2_col2_3, framebuffer_2_col2_4,
       framebuffer_2_col3, framebuffer_2_col3_2, framebuffer_2_col3_3, framebuffer_2_col3_4,
       framebuffer_2_col4, framebuffer_2_col4_2, framebuffer_2_col4_3, framebuffer_2_col4_4,
       framebuffer_2_col5, framebuffer_2_col5_2, framebuffer_2_col5_3, framebuffer_2_col5_4,
       framebuffer_2_col6, framebuffer_2_col6_2, framebuffer_2_col6_3, framebuffer_2_col6_4,
       framebuffer_2_col7, framebuffer_2_col7_2, framebuffer_2_col7_3, framebuffer_2_col7_4,
       framebuffer_3_col0, framebuffer_3_col0_2, framebuffer_3_col0_3, framebuffer_3_col0_4,
       framebuffer_3_col1, framebuffer_3_col1_2, framebuffer_3_col1_3, framebuffer_3_col1_4,
       framebuffer_3_col2, framebuffer_3_col2_2, framebuffer_3_col2_3, framebuffer_3_col2_4,
       framebuffer_3_col3, framebuffer_3_col3_2, framebuffer_3_col3_3, framebuffer_3_col3_4,
       framebuffer_3_col4, framebuffer_3_col4_2, framebuffer_3_col4_3, framebuffer_3_col4_4,
       framebuffer_3_col5, framebuffer_3_col5_2, framebuffer_3_col5_3, framebuffer_3_col5_4,
       framebuffer_3_col6, framebuffer_3_col6_2, framebuffer_3_col6_3, framebuffer_3_col6_4,
       framebuffer_3_col7, framebuffer_3_col7_2, framebuffer_3_col7_3, framebuffer_3_col7_4,
       framebuffer_4_col0, framebuffer_4_col0_2, framebuffer_4_col0_3, framebuffer_4_col0_4,
       framebuffer_4_col1, framebuffer_4_col1_2, framebuffer_4_col1_3, framebuffer_4_col1_4,
       framebuffer_4_col2, framebuffer_4_col2_2, framebuffer_4_col2_3, framebuffer_4_col2_4,
       framebuffer_4_col3, framebuffer_4_col3_2, framebuffer_4_col3_3, framebuffer_4_col3_4,
       framebuffer_4_col4, framebuffer_4_col4_2, framebuffer_4_col4_3, framebuffer_4_col4_4,
       framebuffer_4_col5, framebuffer_4_col5_2, framebuffer_4_col5_3, framebuffer_4_col5_4,
       framebuffer_4_col6, framebuffer_4_col6_2, framebuffer_4_col6_3, framebuffer_4_col6_4,
       framebuffer_4_col7, framebuffer_4_col7_2, framebuffer_4_col7_3, framebuffer_4_col7_4, g32_1_ram_dout,
       memory_be_1_ram_din, rom_1_data;

  not not_1 (not_1_out, in_2);
  Clock clock_1 (.out(clock_1_out));
  Button Reset (.out(Reset_out));
  G32 g32_1 (
    .clk(clock_1_out), .reset(Reset_out), .en(1'b1), .RAM_STB(g32_1_ram_stb), .RAM_WR(g32_1_ram_wr),
    .RAM_ACK(memory_be_1_ram_ack), .RAM_ADDR(g32_1_ram_addr), .RAM_DOUT(g32_1_ram_dout),
    .RAM_DIN(memory_be_1_ram_din), .ROM_ADDR(g32_1_rom_addr), .ROM_DIN(rom_1_data), .RAM_BE(g32_1_ram_be));  // open: en_2
  ROM #(.addrWidth(16), .dataWidth(32)) rom_1 (.addr(g32_1_rom_addr), .data(rom_1_data), .sel(not_1_out));
  ROM #(.addrWidth(16), .dataWidth(32)) rom_2 (.addr(g32_1_rom_addr), .data(rom_1_data), .sel(in_2));
  Memory_BE_Registered memory_be_registered_1 ();  // open: clk, reset, en, RAM_STB, RAM_WR, RAM_BE, RAM_ADDR, RAM_DOUT, RAM_ACK, RAM_DIN
  Memory_BE memory_be_1 (
    .clk(clock_1_out), .reset(Reset_out), .en(1'b1), .RAM_STB(g32_1_ram_stb), .RAM_WR(g32_1_ram_wr),
    .RAM_BE(g32_1_ram_be), .RAM_ADDR(g32_1_ram_addr), .RAM_DOUT(g32_1_ram_dout),
    .RAM_ACK(memory_be_1_ram_ack), .RAM_DIN(memory_be_1_ram_din));
  Clock clock_2 (.out(clock_2_out));
  DotMatrix #(.matrixcols(32), .matrixrows(32)) dotmatrix_1 (
    .col0(framebuffer_1_col0), .col1(framebuffer_1_col1), .col2(framebuffer_1_col2),
    .col3(framebuffer_1_col3), .col4(framebuffer_1_col4), .col5(framebuffer_1_col5),
    .col6(framebuffer_1_col6), .col7(framebuffer_1_col7), .col8(framebuffer_1_col0_2),
    .col9(framebuffer_1_col1_2), .col10(framebuffer_1_col2_2), .col11(framebuffer_1_col3_2),
    .col12(framebuffer_1_col4_2), .col13(framebuffer_1_col5_2), .col14(framebuffer_1_col6_2),
    .col15(framebuffer_1_col7_2), .col16(framebuffer_1_col0_3), .col17(framebuffer_1_col1_3),
    .col18(framebuffer_1_col2_3), .col19(framebuffer_1_col3_3), .col20(framebuffer_1_col4_3),
    .col21(framebuffer_1_col5_3), .col22(framebuffer_1_col6_3), .col23(framebuffer_1_col7_3),
    .col24(framebuffer_1_col0_4), .col25(framebuffer_1_col1_4), .col26(framebuffer_1_col2_4),
    .col27(framebuffer_1_col3_4), .col28(framebuffer_1_col4_4), .col29(framebuffer_1_col5_4),
    .col30(framebuffer_1_col6_4), .col31(framebuffer_1_col7_4));
  FrameBuffer framebuffer_1 (
    .clk(clock_2_out), .RAM_STB(in_3), .RAM_ADDR(in_4), .RAM_DIN(in_5), .Col0(framebuffer_1_col0),
    .Col1(framebuffer_1_col1), .Col2(framebuffer_1_col2), .Col3(framebuffer_1_col3),
    .Col4(framebuffer_1_col4), .Col5(framebuffer_1_col5), .Col6(framebuffer_1_col6),
    .Col7(framebuffer_1_col7), .Col0_2(framebuffer_1_col0_2), .Col1_2(framebuffer_1_col1_2),
    .Col2_2(framebuffer_1_col2_2), .Col3_2(framebuffer_1_col3_2), .Col4_2(framebuffer_1_col4_2),
    .Col5_2(framebuffer_1_col5_2), .Col6_2(framebuffer_1_col6_2), .Col7_2(framebuffer_1_col7_2),
    .Col0_3(framebuffer_1_col0_3), .Col1_3(framebuffer_1_col1_3), .Col2_3(framebuffer_1_col2_3),
    .Col3_3(framebuffer_1_col3_3), .Col4_3(framebuffer_1_col4_3), .Col5_3(framebuffer_1_col5_3),
    .Col6_3(framebuffer_1_col6_3), .Col7_3(framebuffer_1_col7_3), .Col0_4(framebuffer_1_col0_4),
    .Col1_4(framebuffer_1_col1_4), .Col2_4(framebuffer_1_col2_4), .Col3_4(framebuffer_1_col3_4),
    .Col4_4(framebuffer_1_col4_4), .Col5_4(framebuffer_1_col5_4), .Col6_4(framebuffer_1_col6_4),
    .Col7_4(framebuffer_1_col7_4), .FB_Addr_Page_2(framebuffer_1_fb_addr_page_2));  // open: reset, en, RAM_WR, FB_Addr_Page
  DotMatrix #(.matrixcols(32), .matrixrows(32)) dotmatrix_2 (
    .col0(framebuffer_2_col0), .col1(framebuffer_2_col1), .col2(framebuffer_2_col2),
    .col3(framebuffer_2_col3), .col4(framebuffer_2_col4), .col5(framebuffer_2_col5),
    .col6(framebuffer_2_col6), .col7(framebuffer_2_col7), .col8(framebuffer_2_col0_2),
    .col9(framebuffer_2_col1_2), .col10(framebuffer_2_col2_2), .col11(framebuffer_2_col3_2),
    .col12(framebuffer_2_col4_2), .col13(framebuffer_2_col5_2), .col14(framebuffer_2_col6_2),
    .col15(framebuffer_2_col7_2), .col16(framebuffer_2_col0_3), .col17(framebuffer_2_col1_3),
    .col18(framebuffer_2_col2_3), .col19(framebuffer_2_col3_3), .col20(framebuffer_2_col4_3),
    .col21(framebuffer_2_col5_3), .col22(framebuffer_2_col6_3), .col23(framebuffer_2_col7_3),
    .col24(framebuffer_2_col0_4), .col25(framebuffer_2_col1_4), .col26(framebuffer_2_col2_4),
    .col27(framebuffer_2_col3_4), .col28(framebuffer_2_col4_4), .col29(framebuffer_2_col5_4),
    .col30(framebuffer_2_col6_4), .col31(framebuffer_2_col7_4));
  FrameBuffer framebuffer_2 (
    .clk(clock_1_out), .reset(Reset_out), .en(1'b1), .RAM_STB(g32_1_ram_stb), .RAM_WR(g32_1_ram_wr),
    .RAM_ADDR(g32_1_ram_addr[11:0]), .RAM_DIN(g32_1_ram_dout), .FB_Addr_Page(FB_Addr_Page),
    .Col0(framebuffer_2_col0), .Col1(framebuffer_2_col1), .Col2(framebuffer_2_col2),
    .Col3(framebuffer_2_col3), .Col4(framebuffer_2_col4), .Col5(framebuffer_2_col5),
    .Col6(framebuffer_2_col6), .Col7(framebuffer_2_col7), .Col0_2(framebuffer_2_col0_2),
    .Col1_2(framebuffer_2_col1_2), .Col2_2(framebuffer_2_col2_2), .Col3_2(framebuffer_2_col3_2),
    .Col4_2(framebuffer_2_col4_2), .Col5_2(framebuffer_2_col5_2), .Col6_2(framebuffer_2_col6_2),
    .Col7_2(framebuffer_2_col7_2), .Col0_3(framebuffer_2_col0_3), .Col1_3(framebuffer_2_col1_3),
    .Col2_3(framebuffer_2_col2_3), .Col3_3(framebuffer_2_col3_3), .Col4_3(framebuffer_2_col4_3),
    .Col5_3(framebuffer_2_col5_3), .Col6_3(framebuffer_2_col6_3), .Col7_3(framebuffer_2_col7_3),
    .Col0_4(framebuffer_2_col0_4), .Col1_4(framebuffer_2_col1_4), .Col2_4(framebuffer_2_col2_4),
    .Col3_4(framebuffer_2_col3_4), .Col4_4(framebuffer_2_col4_4), .Col5_4(framebuffer_2_col5_4),
    .Col6_4(framebuffer_2_col6_4), .Col7_4(framebuffer_2_col7_4),
    .FB_Addr_Page_2(framebuffer_2_fb_addr_page_2));
  DotMatrix #(.matrixcols(32), .matrixrows(32)) dotmatrix_3 (
    .col0(framebuffer_3_col0), .col1(framebuffer_3_col1), .col2(framebuffer_3_col2),
    .col3(framebuffer_3_col3), .col4(framebuffer_3_col4), .col5(framebuffer_3_col5),
    .col6(framebuffer_3_col6), .col7(framebuffer_3_col7), .col8(framebuffer_3_col0_2),
    .col9(framebuffer_3_col1_2), .col10(framebuffer_3_col2_2), .col11(framebuffer_3_col3_2),
    .col12(framebuffer_3_col4_2), .col13(framebuffer_3_col5_2), .col14(framebuffer_3_col6_2),
    .col15(framebuffer_3_col7_2), .col16(framebuffer_3_col0_3), .col17(framebuffer_3_col1_3),
    .col18(framebuffer_3_col2_3), .col19(framebuffer_3_col3_3), .col20(framebuffer_3_col4_3),
    .col21(framebuffer_3_col5_3), .col22(framebuffer_3_col6_3), .col23(framebuffer_3_col7_3),
    .col24(framebuffer_3_col0_4), .col25(framebuffer_3_col1_4), .col26(framebuffer_3_col2_4),
    .col27(framebuffer_3_col3_4), .col28(framebuffer_3_col4_4), .col29(framebuffer_3_col5_4),
    .col30(framebuffer_3_col6_4), .col31(framebuffer_3_col7_4));
  FrameBuffer framebuffer_3 (
    .clk(clock_2_out), .RAM_STB(in_3), .RAM_ADDR(in_4), .RAM_DIN(in_5),
    .FB_Addr_Page(framebuffer_1_fb_addr_page_2), .Col0(framebuffer_3_col0), .Col1(framebuffer_3_col1),
    .Col2(framebuffer_3_col2), .Col3(framebuffer_3_col3), .Col4(framebuffer_3_col4),
    .Col5(framebuffer_3_col5), .Col6(framebuffer_3_col6), .Col7(framebuffer_3_col7),
    .Col0_2(framebuffer_3_col0_2), .Col1_2(framebuffer_3_col1_2), .Col2_2(framebuffer_3_col2_2),
    .Col3_2(framebuffer_3_col3_2), .Col4_2(framebuffer_3_col4_2), .Col5_2(framebuffer_3_col5_2),
    .Col6_2(framebuffer_3_col6_2), .Col7_2(framebuffer_3_col7_2), .Col0_3(framebuffer_3_col0_3),
    .Col1_3(framebuffer_3_col1_3), .Col2_3(framebuffer_3_col2_3), .Col3_3(framebuffer_3_col3_3),
    .Col4_3(framebuffer_3_col4_3), .Col5_3(framebuffer_3_col5_3), .Col6_3(framebuffer_3_col6_3),
    .Col7_3(framebuffer_3_col7_3), .Col0_4(framebuffer_3_col0_4), .Col1_4(framebuffer_3_col1_4),
    .Col2_4(framebuffer_3_col2_4), .Col3_4(framebuffer_3_col3_4), .Col4_4(framebuffer_3_col4_4),
    .Col5_4(framebuffer_3_col5_4), .Col6_4(framebuffer_3_col6_4), .Col7_4(framebuffer_3_col7_4));  // open: reset, en, RAM_WR, FB_Addr_Page_2
  DotMatrix #(.matrixcols(32), .matrixrows(32)) dotmatrix_4 (
    .col0(framebuffer_4_col0), .col1(framebuffer_4_col1), .col2(framebuffer_4_col2),
    .col3(framebuffer_4_col3), .col4(framebuffer_4_col4), .col5(framebuffer_4_col5),
    .col6(framebuffer_4_col6), .col7(framebuffer_4_col7), .col8(framebuffer_4_col0_2),
    .col9(framebuffer_4_col1_2), .col10(framebuffer_4_col2_2), .col11(framebuffer_4_col3_2),
    .col12(framebuffer_4_col4_2), .col13(framebuffer_4_col5_2), .col14(framebuffer_4_col6_2),
    .col15(framebuffer_4_col7_2), .col16(framebuffer_4_col0_3), .col17(framebuffer_4_col1_3),
    .col18(framebuffer_4_col2_3), .col19(framebuffer_4_col3_3), .col20(framebuffer_4_col4_3),
    .col21(framebuffer_4_col5_3), .col22(framebuffer_4_col6_3), .col23(framebuffer_4_col7_3),
    .col24(framebuffer_4_col0_4), .col25(framebuffer_4_col1_4), .col26(framebuffer_4_col2_4),
    .col27(framebuffer_4_col3_4), .col28(framebuffer_4_col4_4), .col29(framebuffer_4_col5_4),
    .col30(framebuffer_4_col6_4), .col31(framebuffer_4_col7_4));
  FrameBuffer framebuffer_4 (
    .clk(clock_1_out), .reset(Reset_out), .en(1'b1), .RAM_STB(g32_1_ram_stb), .RAM_WR(g32_1_ram_wr),
    .RAM_ADDR(g32_1_ram_addr[11:0]), .RAM_DIN(g32_1_ram_dout), .FB_Addr_Page(framebuffer_2_fb_addr_page_2),
    .Col0(framebuffer_4_col0), .Col1(framebuffer_4_col1), .Col2(framebuffer_4_col2),
    .Col3(framebuffer_4_col3), .Col4(framebuffer_4_col4), .Col5(framebuffer_4_col5),
    .Col6(framebuffer_4_col6), .Col7(framebuffer_4_col7), .Col0_2(framebuffer_4_col0_2),
    .Col1_2(framebuffer_4_col1_2), .Col2_2(framebuffer_4_col2_2), .Col3_2(framebuffer_4_col3_2),
    .Col4_2(framebuffer_4_col4_2), .Col5_2(framebuffer_4_col5_2), .Col6_2(framebuffer_4_col6_2),
    .Col7_2(framebuffer_4_col7_2), .Col0_3(framebuffer_4_col0_3), .Col1_3(framebuffer_4_col1_3),
    .Col2_3(framebuffer_4_col2_3), .Col3_3(framebuffer_4_col3_3), .Col4_3(framebuffer_4_col4_3),
    .Col5_3(framebuffer_4_col5_3), .Col6_3(framebuffer_4_col6_3), .Col7_3(framebuffer_4_col7_3),
    .Col0_4(framebuffer_4_col0_4), .Col1_4(framebuffer_4_col1_4), .Col2_4(framebuffer_4_col2_4),
    .Col3_4(framebuffer_4_col3_4), .Col4_4(framebuffer_4_col4_4), .Col5_4(framebuffer_4_col5_4),
    .Col6_4(framebuffer_4_col6_4), .Col7_4(framebuffer_4_col7_4),
    .FB_Addr_Page_2(framebuffer_4_fb_addr_page_2));
  // Pins of 12 and 16 bits meet at g32_1_ram_addr
endmodule

module G32 (
  input  clk,
  input  reset,
  input  en,
  input  [31:0] ROM_DIN,
  input  RAM_ACK,
  input  [31:0] RAM_DIN,
  input  en_2,
  output [15:0] ROM_ADDR,
  output [3:0] RAM_BE,
  output RAM_STB,
  output RAM_WR,
  output [15:0] RAM_ADDR,
  output [31:0] RAM_DOUT
);

  wire g32_id_1_alu_is_lea, g32_id_1_alu_sel_imm, g32_id_1_ldr_ram, g32_id_1_ra_is_rd, g32_id_1_rf_wb,
       g32_memc_1_p3, g32_memc_1_p9, g32_memc_1_p15, g32_memc_1_p21, g32_memc_1_p27, g32_memc_1_p33,
       g32_memc_1_p39, g32_memc_1_p45, g32_memc_1_p51, g32_memc_1_p57, g32_memc_1_p59, g32_memc_1_p60,
       g32_thread_1_exec_mask_next, g32_thread_1_lds_stb, g32_thread_1_lds_wr, g32_thread_1_ram_stb,
       g32_thread_1_ram_wr, g32_thread_2_lds_stb, g32_thread_2_lds_wr, g32_thread_2_ram_stb,
       g32_thread_2_ram_wr, g32_thread_3_lds_stb, g32_thread_3_lds_wr, g32_thread_3_ram_stb,
       g32_thread_3_ram_wr, g32_thread_4_lds_stb, g32_thread_4_lds_wr, g32_thread_4_ram_stb,
       g32_thread_4_ram_wr, g32_thread_5_lds_stb, g32_thread_5_lds_wr, g32_thread_5_ram_stb,
       g32_thread_5_ram_wr, register_7_q, register_8_q, register_10_q, register_11_q, undriven_3, undriven_6,
       undriven_7, undriven_8, undriven_10, undriven_14, undriven_15, undriven_20, undriven_22, undriven_24;
  wire [1:0] g32_controller_1_hyperthread_id, g32_thread_2_lane_id_out, g32_thread_3_lane_id_out,
       g32_thread_4_lane_id_out, g32_thread_5_lane_id_out, pull_resistor_1_node, undriven_2;
  wire [2:0] g32_id_pre_1_predicate, register_6_q, register_15_q, register_16_q, register_19_q, undriven_5,
       undriven_27;
  wire [3:0] g32_controller_1_exec_mask_out, g32_id_1_alu_cmd, register_9_q, undriven, undriven_9,
       undriven_26, undriven_28;
  wire [4:0] g32_id_pre_1_ra, g32_id_pre_1_rb, g32_id_pre_1_rd, multiplexer_1_out, register_2_q,
       register_3_q, register_4_q, register_12_q, register_13_q, register_14_q, undriven_11, undriven_12,
       undriven_13;
  wire [7:0] g32_id_pre_1_opcode, register_5_q;
  wire [9:0] g32_memc_1_p61, g32_thread_1_lds_addr, g32_thread_2_lds_addr, g32_thread_3_lds_addr,
       g32_thread_4_lds_addr, g32_thread_5_lds_addr;
  wire [11:0] g32_thread_1_ram_addr, g32_thread_2_ram_addr, g32_thread_3_ram_addr, g32_thread_4_ram_addr,
       g32_thread_5_ram_addr;
  wire [11:10] register_18_q;
  wire [15:0] g32_controller_1_grid_x, g32_controller_1_grid_x_n_2, g32_controller_1_grid_y,
       g32_controller_1_grid_y_n_2, g32_controller_1_wg_x, g32_controller_1_wg_x_n_2, g32_controller_1_wg_y,
       g32_controller_1_wg_y_n_2, undriven_16, undriven_17, undriven_18, undriven_19, undriven_21;
  wire [20:0] g32_id_pre_1_predec_instruction, register_1_q;
  wire [31:0] g32_id_1_imm, g32_memc_1_p4, g32_memc_1_p10, g32_memc_1_p16, g32_memc_1_p22, g32_memc_1_p28,
       g32_memc_1_p34, g32_memc_1_p40, g32_memc_1_p46, g32_memc_1_p58, g32_memc_1_p62, g32_thread_1_lds_dout,
       g32_thread_1_ram_dout, g32_thread_2_lds_dout, g32_thread_2_ram_dout, g32_thread_3_lds_dout,
       g32_thread_3_ram_dout, g32_thread_4_lds_dout, g32_thread_4_ram_dout, g32_thread_5_lds_dout,
       g32_thread_5_ram_dout, register_17_q, undriven_4, undriven_23, undriven_25;

  G32_ID_Pre g32_id_pre_1 (
    .instruction(ROM_DIN), .predec_instruction(g32_id_pre_1_predec_instruction), .rb(g32_id_pre_1_rb),
    .ra(g32_id_pre_1_ra), .rd(g32_id_pre_1_rd), .opcode(g32_id_pre_1_opcode),
    .predicate(g32_id_pre_1_predicate));
  // Probe on ROM_ADDR
  Register #(.width(21)) register_1 (
    .D(g32_id_pre_1_predec_instruction), .en(en), .Q(register_1_q), .clk(clk), .clr(reset));
  Register #(.width(5)) register_2 (.D(g32_id_pre_1_rb), .en(en), .Q(register_2_q), .clk(clk), .clr(reset));
  Register #(.width(5)) register_3 (.D(g32_id_pre_1_ra), .en(en), .Q(register_3_q), .clk(clk), .clr(reset));
  Register #(.width(5)) register_4 (.D(g32_id_pre_1_rd), .en(en), .Q(register_4_q), .clk(clk), .clr(reset));
  Register register_5 (.D(g32_id_pre_1_opcode), .en(en), .Q(register_5_q), .clk(clk), .clr(reset));
  Register #(.width(3)) register_6 (.D(g32_id_pre_1_predicate), .en(en), .Q(register_6_q), .clk(clk), .clr(reset));
  G32_IF g32_if_1 (.imem_addr(ROM_ADDR), .clk(clk), .reset(reset), .en(en));
  G32_THREAD g32_thread_1 (
    .clk(undriven_15), .reset(undriven_14), .en(undriven_3), .rd(undriven_13), .rb(undriven_12),
    .ra(undriven_11), .tid(undriven_2), .imm(undriven_4), .rf_wr(undriven_10),
    .RAM_ADDR(g32_thread_1_ram_addr), .RAM_WR(g32_thread_1_ram_wr), .RAM_DIN(undriven_23),
    .RAM_DOUT(g32_thread_1_ram_dout), .LDS_ADDR(g32_thread_1_lds_addr), .LDS_WR(g32_thread_1_lds_wr),
    .LDS_DIN(undriven_25), .LDS_DOUT(g32_thread_1_lds_dout), .LDS_STALL(undriven_24),
    .RAM_STALL(undriven_22), .RAM_STB(g32_thread_1_ram_stb), .LDS_STB(g32_thread_1_lds_stb),
    .predicate(undriven_5), .alu_is_lea(undriven_8), .alu_sel_imm(undriven_7), .alu_cmd(undriven_9),
    .ldr_ram(undriven_6), .wg_x(undriven_16), .wg_y(undriven_17), .wg_x_2(undriven_18), .wg_y_2(undriven_19),
    .exec_mask_next(g32_thread_1_exec_mask_next), .exec_mask(undriven), .grid_x_n(undriven_21));  // open: lane_id_in, lane_id_out, wg_x_n, wg_y_n, grid_y_n, RAM_BE, LDS_BE
  // Probe on register_1_q
  // Probe on register_5_q
  G32_ID g32_id_1 (
    .predec_instruction(register_1_q), .opcode(register_5_q), .imm(g32_id_1_imm), .rf_wb(g32_id_1_rf_wb),
    .alu_cmd(g32_id_1_alu_cmd), .alu_is_lea(g32_id_1_alu_is_lea), .alu_sel_imm(g32_id_1_alu_sel_imm),
    .ldr_ram(g32_id_1_ldr_ram), .ra_is_rd(g32_id_1_ra_is_rd));
  // Probe on undriven_20
  // Probe on register_2_q
  Multiplexer #(.width(5), .disabled(0), .enable("false")) multiplexer_1 (
    .in0(register_3_q), .in1(register_4_q), .out(multiplexer_1_out), .sel(g32_id_1_ra_is_rd));
  // Probe on multiplexer_1_out
  // Probe on register_4_q
  // Probe on register_6_q
  G32_Controller g32_controller_1 (
    .clk(clk), .reset(reset), .en(en), .exec_mask_in(undriven_28), .wg_x(g32_controller_1_wg_x),
    .wg_y(g32_controller_1_wg_y), .grid_x(g32_controller_1_grid_x), .grid_y(g32_controller_1_grid_y),
    .hyperthread_id(g32_controller_1_hyperthread_id), .exec_mask_out(g32_controller_1_exec_mask_out),
    .halt_mask_in(undriven_26), .wg_x_n_2(g32_controller_1_wg_x_n_2), .wg_y_n_2(g32_controller_1_wg_y_n_2),
    .grid_x_n_2(g32_controller_1_grid_x_n_2), .grid_y_n_2(g32_controller_1_grid_y_n_2), .wg_x_n(16'h1),
    .wg_y_n({16{1'b0}}), .grid_x_n({16{1'b0}}), .grid_y_n({16{1'b0}}), .start(en_2));  // open: reset_2
  Register #(.width(1)) register_7 (.D(g32_id_1_ldr_ram), .en(en), .Q(register_7_q), .clk(clk), .clr(reset));
  Register #(.width(1)) register_8 (.D(g32_id_1_rf_wb), .en(en), .Q(register_8_q), .clk(clk), .clr(reset));
  Register #(.width(4)) register_9 (.D(g32_id_1_alu_cmd), .en(en), .Q(register_9_q), .clk(clk), .clr(reset));
  Register #(.width(1)) register_10 (.D(g32_id_1_alu_is_lea), .en(en), .Q(register_10_q), .clk(clk), .clr(reset));
  Register #(.width(1)) register_11 (.D(g32_id_1_alu_sel_imm), .en(en), .Q(register_11_q), .clk(clk), .clr(reset));
  Register #(.width(5)) register_12 (.D(register_2_q), .en(en), .Q(register_12_q), .clk(clk), .clr(reset));
  Register #(.width(5)) register_13 (.D(multiplexer_1_out), .en(en), .Q(register_13_q), .clk(clk), .clr(reset));
  Register #(.width(5)) register_14 (.D(register_4_q), .en(en), .Q(register_14_q), .clk(clk), .clr(reset));
  Register #(.width(3)) register_15 (.en(en), .Q(register_15_q), .clk(clk), .clr(reset));  // open: D
  Register #(.width(3)) register_16 (.D(register_6_q), .en(en), .Q(register_16_q), .clk(clk), .clr(reset));
  Register #(.width(32)) register_17 (.D(g32_id_1_imm), .en(en), .Q(register_17_q), .clk(clk), .clr(reset));
  Register #(.width(2)) register_18 (
    .D(g32_controller_1_hyperthread_id), .en(en), .Q(register_18_q), .clk(clk), .clr(reset));
  Register #(.width(3)) register_19 (.D(undriven_27), .en(en), .Q(register_19_q), .clk(clk), .clr(reset));
  // Probe on register_8_q
  // Probe on register_9_q
  // Probe on register_10_q
  // Probe on register_11_q
  // Probe on register_12_q
  // Probe on register_13_q
  // Probe on register_14_q
  // Probe on register_16_q
  // Probe on register_17_q
  // Probe on register_18_q
  // Probe on undriven_28
  G32_THREAD g32_thread_2 (
    .clk(clk), .reset(reset), .en(undriven_28[0]), .rd(register_14_q), .rb(register_12_q),
    .ra(register_13_q), .tid(register_18_q), .imm(register_17_q), .rf_wr(register_8_q),
    .lane_id_in(pull_resistor_1_node), .lane_id_out(g32_thread_2_lane_id_out),
    .RAM_ADDR(g32_thread_2_ram_addr), .RAM_WR(g32_thread_2_ram_wr), .RAM_DIN(g32_memc_1_p4),
    .RAM_DOUT(g32_thread_2_ram_dout), .LDS_ADDR(g32_thread_2_lds_addr), .LDS_WR(g32_thread_2_lds_wr),
    .LDS_DIN(g32_memc_1_p10), .LDS_DOUT(g32_thread_2_lds_dout), .LDS_STALL(g32_memc_1_p9),
    .RAM_STALL(g32_memc_1_p3), .RAM_STB(g32_thread_2_ram_stb), .LDS_STB(g32_thread_2_lds_stb),
    .predicate(register_19_q), .alu_is_lea(register_10_q), .alu_sel_imm(register_11_q),
    .alu_cmd(register_9_q), .ldr_ram(register_7_q), .wg_x(g32_controller_1_grid_y),
    .wg_y(g32_controller_1_grid_x), .wg_x_2(g32_controller_1_wg_y), .wg_y_2(g32_controller_1_wg_x),
    .exec_mask_next(g32_controller_1_exec_mask_out[3]), .wg_x_n(g32_controller_1_grid_y_n_2),
    .wg_y_n(g32_controller_1_grid_x_n_2), .grid_x_n(g32_controller_1_wg_y_n_2),
    .grid_y_n(g32_controller_1_wg_x_n_2));  // open: exec_mask, RAM_BE, LDS_BE
  G32_THREAD g32_thread_3 (
    .clk(clk), .reset(reset), .en(undriven_28[1]), .rd(register_14_q), .rb(register_12_q),
    .ra(register_13_q), .tid(register_18_q), .imm(register_17_q), .rf_wr(register_8_q),
    .lane_id_in(g32_thread_2_lane_id_out), .lane_id_out(g32_thread_3_lane_id_out),
    .RAM_ADDR(g32_thread_3_ram_addr), .RAM_WR(g32_thread_3_ram_wr), .RAM_DIN(g32_memc_1_p16),
    .RAM_DOUT(g32_thread_3_ram_dout), .LDS_ADDR(g32_thread_3_lds_addr), .LDS_WR(g32_thread_3_lds_wr),
    .LDS_DIN(g32_memc_1_p22), .LDS_DOUT(g32_thread_3_lds_dout), .LDS_STALL(g32_memc_1_p21),
    .RAM_STALL(g32_memc_1_p15), .RAM_STB(g32_thread_3_ram_stb), .LDS_STB(g32_thread_3_lds_stb),
    .predicate(register_19_q), .alu_is_lea(register_10_q), .alu_sel_imm(register_11_q),
    .alu_cmd(register_9_q), .ldr_ram(register_7_q), .wg_x(g32_controller_1_grid_y),
    .wg_y(g32_controller_1_grid_x), .wg_x_2(g32_controller_1_wg_y), .wg_y_2(g32_controller_1_wg_x),
    .exec_mask_next(g32_controller_1_exec_mask_out[2]), .exec_mask(undriven_28),
    .wg_x_n(g32_controller_1_grid_y_n_2), .wg_y_n(g32_controller_1_grid_x_n_2),
    .grid_x_n(g32_controller_1_wg_y_n_2), .grid_y_n(g32_controller_1_wg_x_n_2));  // open: RAM_BE, LDS_BE
  G32_THREAD g32_thread_4 (
    .clk(clk), .reset(reset), .en(undriven_28[2]), .rd(register_14_q), .rb(register_12_q),
    .ra(register_13_q), .tid(register_18_q), .imm(register_17_q), .rf_wr(register_8_q),
    .lane_id_in(g32_thread_3_lane_id_out), .lane_id_out(g32_thread_4_lane_id_out),
    .RAM_ADDR(g32_thread_4_ram_addr), .RAM_WR(g32_thread_4_ram_wr), .RAM_DIN(g32_memc_1_p28),
    .RAM_DOUT(g32_thread_4_ram_dout), .LDS_ADDR(g32_thread_4_lds_addr), .LDS_WR(g32_thread_4_lds_wr),
    .LDS_DIN(g32_memc_1_p34), .LDS_DOUT(g32_thread_4_lds_dout), .LDS_STALL(g32_memc_1_p33),
    .RAM_STALL(g32_memc_1_p27), .RAM_STB(g32_thread_4_ram_stb), .LDS_STB(g32_thread_4_lds_stb),
    .predicate(register_19_q), .alu_is_lea(register_10_q), .alu_sel_imm(register_11_q),
    .alu_cmd(register_9_q), .ldr_ram(register_7_q), .wg_x(g32_controller_1_grid_y),
    .wg_y(g32_controller_1_grid_x), .wg_x_2(g32_controller_1_wg_y), .wg_y_2(g32_controller_1_wg_x),
    .exec_mask_next(g32_controller_1_exec_mask_out[1]), .exec_mask(undriven_28),
    .wg_x_n(g32_controller_1_grid_y_n_2), .wg_y_n(g32_controller_1_grid_x_n_2),
    .grid_x_n(g32_controller_1_wg_y_n_2), .grid_y_n(g32_controller_1_wg_x_n_2));  // open: RAM_BE, LDS_BE
  G32_THREAD g32_thread_5 (
    .clk(clk), .reset(reset), .en(undriven_28[3]), .rd(register_14_q), .rb(register_12_q),
    .ra(register_13_q), .tid(register_18_q), .imm(register_17_q), .rf_wr(register_8_q),
    .lane_id_in(g32_thread_4_lane_id_out), .lane_id_out(g32_thread_5_lane_id_out),
    .RAM_ADDR(g32_thread_5_ram_addr), .RAM_WR(g32_thread_5_ram_wr), .RAM_DIN(g32_memc_1_p40),
    .RAM_DOUT(g32_thread_5_ram_dout), .LDS_ADDR(g32_thread_5_lds_addr), .LDS_WR(g32_thread_5_lds_wr),
    .LDS_DIN(g32_memc_1_p46), .LDS_DOUT(g32_thread_5_lds_dout), .LDS_STALL(g32_memc_1_p45),
    .RAM_STALL(g32_memc_1_p39), .RAM_STB(g32_thread_5_ram_stb), .LDS_STB(g32_thread_5_lds_stb),
    .predicate(register_19_q), .alu_is_lea(register_10_q), .alu_sel_imm(register_11_q),
    .alu_cmd(register_9_q), .ldr_ram(register_7_q), .wg_x(g32_controller_1_grid_y),
    .wg_y(g32_controller_1_grid_x), .wg_x_2(g32_controller_1_wg_y), .wg_y_2(g32_controller_1_wg_x),
    .exec_mask_next(g32_controller_1_exec_mask_out[0]), .exec_mask(undriven_28),
    .wg_x_n(g32_controller_1_grid_y_n_2), .wg_y_n(g32_controller_1_grid_x_n_2),
    .grid_x_n(g32_controller_1_wg_y_n_2), .grid_y_n(g32_controller_1_wg_x_n_2));  // open: RAM_BE, LDS_BE
  // Probe on g32_controller_1_exec_mask_out
  Pull_Resistor pull_resistor_1 (.node(pull_resistor_1_node));
  // Probe on pull_resistor_1_node
  // Probe on g32_thread_2_lane_id_out
  // Probe on g32_thread_3_lane_id_out
  // Probe on g32_thread_4_lane_id_out
  // G32_MEMC g32_memc_1: pin names not known; wires that end beside it: clk, reset, g32_memc_1_p3, g32_memc_1_p4, g32_thread_2_ram_stb, g32_thread_2_ram_wr, g32_thread_2_ram_addr, g32_thread_2_ram_dout, g32_memc_1_p9, g32_memc_1_p10, g32_thread_2_lds_stb, g32_thread_2_lds_wr, g32_thread_2_lds_addr, g32_thread_2_lds_dout, g32_memc_1_p15, g32_memc_1_p16, g32_thread_3_ram_stb, g32_thread_3_ram_wr, g32_thread_3_ram_addr, g32_thread_3_ram_dout, g32_memc_1_p21, g32_memc_1_p22, g32_thread_3_lds_stb, g32_thread_3_lds_wr, g32_thread_3_lds_addr, g32_thread_3_lds_dout, g32_memc_1_p27, g32_memc_1_p28, g32_thread_4_ram_stb, g32_thread_4_ram_wr, g32_thread_4_ram_addr, g32_thread_4_ram_dout, g32_memc_1_p33, g32_memc_1_p34, g32_thread_4_lds_stb, g32_thread_4_lds_wr, g32_thread_4_lds_addr, g32_thread_4_lds_dout, g32_memc_1_p39, g32_memc_1_p40, g32_thread_5_ram_stb, g32_thread_5_ram_wr, g32_thread_5_ram_addr, g32_thread_5_ram_dout, g32_memc_1_p45, g32_memc_1_p46, g32_thread_5_lds_stb, g32_thread_5_lds_wr, g32_thread_5_lds_addr, g32_thread_5_lds_dout, g32_memc_1_p51, RAM_DOUT, RAM_STB, RAM_WR, RAM_ADDR, RAM_DIN, g32_memc_1_p57, g32_memc_1_p58, g32_memc_1_p59, g32_memc_1_p60, g32_memc_1_p61, g32_memc_1_p62, RAM_BE
  Register #(.width(1)) register_20 (.D(g32_memc_1_p59), .Q(g32_memc_1_p57), .clk(clk), .clr(reset));  // open: en
  RAM #(.addrWidth(12), .dataWidth(32), .bus("separate")) ram_1 (
    .addr({register_18_q, g32_memc_1_p61}), .din(g32_memc_1_p62), .data(g32_memc_1_p58),
    .str(g32_memc_1_p60), .clk(clk));  // open: sel, ld, clr

  // Notes on the sheet:
  //   en_2: pull=up
  //   en: pull=up
  //   IMEM
  //   Missing:
  //   Memory I/O
  //   LEA
  //   See LSU UNIT
  //   Interconnect
  //   Immediate decoding
  //   Any jumping/branching
  //   ThreadId latency incorrect for RAM/LDS
  //   Flag upgate gates
  //   Invo register
  //   WG invos count full lane invocations
  //   DMEM (RAM)
  //   DMEM (LDS)
endmodule

module G32_IF (
  input  clk,
  input  reset,
  input  en,
  output [15:0] imem_addr
);

  wire comparator_1_eq, or_1_out;
  wire [15:0] adder_1_out;

  or or_1 (or_1_out, reset, comparator_1_eq);
  Register #(.width(16)) register_1 (.D(adder_1_out), .en(en), .Q(imem_addr), .clk(clk), .clr(or_1_out));
  Adder #(.width(16)) adder_1 (.a(imem_addr), .b(16'h1), .out(adder_1_out));  // open: cin, cout
  Comparator #(.width(16)) comparator_1 (.a(imem_addr), .b(16'hb), .eq(comparator_1_eq));  // open: gt, lt
endmodule

module G32_ID_Pre (
  input  [31:0] instruction,
  output [20:0] predec_instruction,
  output [4:0] rb,
  output [4:0] ra,
  output [4:0] rd,
  output [2:0] predicate,
  output [7:0] opcode
);

  // Probe on instruction[10:6]
  // Probe on instruction[15:11]
  // Probe on instruction[20:16]

  assign opcode = instruction[31:24];
  assign predec_instruction = instruction[20:0];
  assign predicate = instruction[23:21];
  assign ra = instruction[15:11];
  assign rb = instruction[10:6];
  assign rd = instruction[20:16];
endmodule

module G32_ID (
  input  [20:0] predec_instruction,
  input  [7:0] opcode,
  output alu_is_lea,
  output alu_sel_imm,
  output [31:0] imm,
  output [3:0] alu_cmd,
  output rf_wb,
  output ra_is_rd,
  output ldr_ram
);

  wire comparator_1_eq, comparator_2_eq, comparator_3_eq, comparator_3_lt, comparator_4_eq, comparator_5_eq,
       comparator_5_lt, comparator_6_eq, or_1_out, or_3_out, or_5_out, or_6_out, pull_resistor_8_node,
       pull_resistor_9_node;
  wire [3:0] multiplexer_1_out, pull_resistor_7_node;
  wire [3:3] pull_resistor_1_node;
  wire [15:0] multiplexer_2_out, multiplexer_3_out, pull_resistor_2_node, pull_resistor_3_node;
  wire [31:0] multiplexer_4_out, pull_resistor_4_node, pull_resistor_6_node;

  // Probe on predec_instruction[15:0]
  Comparator #(.width(4)) comparator_1 (.a(opcode[7:4]), .b(4'b0000), .eq(comparator_1_eq));  // open: gt, lt
  Comparator #(.width(4)) comparator_2 (.a(opcode[7:4]), .b(4'b0001), .eq(comparator_2_eq));  // open: gt, lt
  Comparator comparator_3 (.a(opcode), .b(8'h80), .eq(comparator_3_eq), .lt(comparator_3_lt));  // open: gt
  Comparator comparator_4 (.a(opcode), .b(8'h81), .eq(comparator_4_eq));  // open: gt, lt
  Comparator comparator_5 (.a(opcode), .b(8'h84), .eq(comparator_5_eq), .lt(comparator_5_lt));  // open: gt
  Comparator comparator_6 (.a(opcode), .b(8'h85), .eq(comparator_6_eq));  // open: gt, lt
  Pull_Resistor pull_resistor_1 (.node(pull_resistor_1_node[3]));
  Pull_Resistor pull_resistor_2 (.node(pull_resistor_2_node));
  Pull_Resistor pull_resistor_3 (.node(pull_resistor_3_node));
  Multiplexer #(.width(4), .disabled(0), .enable("false")) multiplexer_1 (
    .in0({pull_resistor_1_node[3], opcode[2:0]}), .in1(opcode[3:0]), .out(multiplexer_1_out),
    .sel(comparator_1_eq));
  Multiplexer #(.width(16), .disabled(0), .enable("false")) multiplexer_2 (
    .in0(pull_resistor_2_node), .in1(predec_instruction[15:0]), .out(multiplexer_2_out), .sel(comparator_3_eq));
  Multiplexer #(.width(16), .disabled(0), .enable("false")) multiplexer_3 (
    .in0(pull_resistor_3_node), .in1(predec_instruction[15:0]), .out(multiplexer_3_out), .sel(comparator_4_eq));
  or or_1 (or_1_out, comparator_3_eq, comparator_4_eq);
  // Probe on {multiplexer_3_out, multiplexer_2_out}
  Multiplexer #(.width(32), .disabled(0), .enable("false")) multiplexer_4 (
    .in0({multiplexer_3_out, multiplexer_2_out}), .in1(pull_resistor_4_node), .out(multiplexer_4_out),
    .sel(comparator_2_eq));
  Pull_Resistor #(.pull("X")) pull_resistor_4 (.node(pull_resistor_4_node));
  or or_2 (alu_sel_imm, or_1_out, comparator_2_eq);
  or or_3 (or_3_out, comparator_1_eq, comparator_2_eq);
  or or_4 (ra_is_rd, comparator_3_eq, comparator_4_eq);
  Pull_Resistor pull_resistor_5 (.node(alu_is_lea));
  Pull_Resistor #(.pull("X")) pull_resistor_6 (.node(pull_resistor_6_node));
  Multiplexer #(.width(32), .disabled(0), .enable("false")) multiplexer_5 (
    .in0(pull_resistor_6_node), .in1(multiplexer_4_out), .out(imm), .sel(alu_sel_imm));
  Pull_Resistor pull_resistor_7 (.node(pull_resistor_7_node));
  Multiplexer #(.width(4), .disabled(0), .enable("false")) multiplexer_6 (
    .in0(pull_resistor_7_node), .in1(multiplexer_1_out), .out(alu_cmd), .sel(or_5_out));
  or or_5 (or_5_out, or_3_out, pull_resistor_8_node);
  Pull_Resistor pull_resistor_8 (.node(pull_resistor_8_node));
  or or_6 (or_6_out, or_3_out, ra_is_rd);
  Pull_Resistor pull_resistor_9 (.node(pull_resistor_9_node));
  or or_7 (rf_wb, or_6_out, comparator_5_eq, pull_resistor_9_node);
  Pull_Resistor #(.pull("X")) pull_resistor_10 (.node(ldr_ram));

  // Notes on the sheet:
  //   LLI
  //   LUI
  //   LD
  //   ST
  //   extended ALU ops restriced to not imm
  //   ALU
  //   ALUI
  //   ALU
  //   ALUI
  //   LLI
  //   LUI
  //   LD
  //   ST
endmodule

module G32_MEMC (
  input  clk,
  input  reset,
  input  [3:0] RAM_BE,
  input  RAM_STB,
  input  RAM_WR,
  input  RAM_ACK,
  input  [11:0] RAM_ADDR,
  input  [31:0] RAM_DOUT,
  input  [31:0] RAM_DIN,
  input  [3:0] LDS_BE,
  input  LDS_STB,
  input  LDS_WR,
  input  LDS_ACK,
  input  [9:0] LDS_ADDR,
  input  [31:0] LDS_DOUT,
  input  [31:0] LDS_DIN,
  input  RAM_STB_2,
  input  RAM_WR_2,
  input  [11:0] RAM_ADDR_2,
  input  [31:0] RAM_DOUT_2,
  input  LDS_STB_2,
  input  LDS_WR_2,
  input  [9:0] LDS_ADDR_2,
  input  [31:0] LDS_DOUT_2,
  input  RAM_STB_3,
  input  RAM_WR_3,
  input  [11:0] RAM_ADDR_3,
  input  [31:0] RAM_DOUT_3,
  input  LDS_STB_3,
  input  LDS_WR_3,
  input  [9:0] LDS_ADDR_3,
  input  [31:0] LDS_DOUT_3,
  input  RAM_STB_4,
  input  RAM_WR_4,
  input  [11:0] RAM_ADDR_4,
  input  [31:0] RAM_DOUT_4,
  input  LDS_STB_4,
  input  LDS_WR_4,
  input  [9:0] LDS_ADDR_4,
  input  [31:0] RAM_DOUT_5,
  output [3:0] RAM_BE_2,
  output RAM_STB_5,
  output RAM_WR_5,
  output RAM_ACK_2,
  output [11:0] RAM_ADDR_5,
  output [31:0] RAM_DOUT_6,
  output [31:0] RAM_DIN_2,
  output [3:0] LDS_BE_2,
  output LDS_STB_5,
  output LDS_WR_5,
  output LDS_ACK_2,
  output [9:0] LDS_ADDR_5,
  output [31:0] LDS_DOUT_4,
  output [31:0] LDS_DIN_2,
  output RAM_STALL,
  output [31:0] RAM_DIN_3,
  output LDS_STALL,
  output [31:0] LDS_DIN_3,
  output RAM_STALL_2,
  output [31:0] RAM_DIN_4,
  output LDS_STALL_2,
  output [31:0] LDS_DIN_4,
  output RAM_STALL_3,
  output [31:0] RAM_DIN_5,
  output LDS_STALL_3,
  output [31:0] LDS_DIN_5
);

  G32_MEMC_Combiner g32_memc_combiner_1 ();  // open: clk, reset, en, STB_A, STB_B, A_WR, B_WR, ADDR_A, ADDR_B, A_BE, A_DOUT, B_BE, B_DOUT, RAM_DIN, RAM_DIN_2, did_combine, combined_BE, combined_DOUT_2, combined_DOUT

  assign LDS_ACK_2 = LDS_ACK;
  assign LDS_ADDR_5 = LDS_ADDR;
  assign LDS_BE_2 = LDS_BE;
  assign LDS_DIN_2 = LDS_DIN;
  assign LDS_DOUT_4 = LDS_DOUT;
  assign LDS_STB_5 = LDS_STB;
  assign LDS_WR_5 = LDS_WR;
  assign RAM_ACK_2 = RAM_ACK;
  assign RAM_ADDR_5 = RAM_ADDR;
  assign RAM_BE_2 = RAM_BE;
  assign RAM_DIN_2 = RAM_DIN;
  assign RAM_DOUT_6 = RAM_DOUT;
  assign RAM_STB_5 = RAM_STB;
  assign RAM_WR_5 = RAM_WR;

  // Notes on the sheet:
  //   BE
endmodule

module G32_MEMC_Combiner (
  input  clk,
  input  reset,
  input  en,
  input  STB_A,
  input  STB_B,
  input  A_WR,
  input  B_WR,
  input  [11:0] ADDR_A,
  input  [11:0] ADDR_B,
  input  [3:0] A_BE,
  input  [31:0] A_DOUT,
  input  [3:0] B_BE,
  input  [31:0] B_DOUT,
  input  [31:0] combined_DOUT,
  output did_combine,
  output [3:0] combined_BE,
  output [31:0] combined_DOUT_2,
  output [31:0] RAM_DIN,
  output [31:0] RAM_DIN_2
);

  wire and_1_out, and_2_out, and_3_out, comparator_1_eq, comparator_2_eq;
  wire [3:0] pull_resistor_1_node;

  and and_1 (and_1_out, STB_A, STB_B);
  and and_2 (and_2_out, A_WR, B_WR);
  Comparator #(.width(12)) comparator_1 (.a(ADDR_A), .b(ADDR_B), .eq(comparator_1_eq));  // open: gt, lt
  and and_3 (and_3_out, en, and_1_out, and_2_out, comparator_1_eq);
  Pull_Resistor pull_resistor_1 (.node(pull_resistor_1_node));
  G32_MEMC_C_ByteLane g32_memc_c_bytelane_1 (
    .A_BE(A_BE[0]), .B_BE(B_BE[0]), .A_DIN(A_DOUT[7:0]), .B_DIN(B_DOUT[7:0]),
    .combined_DOUT(combined_DOUT_2[7:0]), .combined_BE(combined_BE[0]));
  G32_MEMC_C_ByteLane g32_memc_c_bytelane_2 (
    .A_BE(A_BE[1]), .B_BE(B_BE[1]), .A_DIN(A_DOUT[15:8]), .B_DIN(B_DOUT[15:8]),
    .combined_DOUT(combined_DOUT_2[15:8]), .combined_BE(combined_BE[1]));
  G32_MEMC_C_ByteLane g32_memc_c_bytelane_3 (
    .A_BE(A_BE[2]), .B_BE(B_BE[2]), .A_DIN(A_DOUT[23:16]), .B_DIN(B_DOUT[23:16]),
    .combined_DOUT(combined_DOUT_2[23:16]), .combined_BE(combined_BE[2]));
  G32_MEMC_C_ByteLane g32_memc_c_bytelane_4 (
    .A_BE(A_BE[3]), .B_BE(B_BE[3]), .A_DIN(A_DOUT[31:24]), .B_DIN(B_DOUT[31:24]),
    .combined_DOUT(combined_DOUT_2[31:24]), .combined_BE(combined_BE[3]));
  and and_4 (did_combine, and_3_out, ~comparator_2_eq);  // AND_Gate
  Comparator #(.width(4)) comparator_2 (
    .a(pull_resistor_1_node), .b(combined_BE), .eq(comparator_2_eq));  // open: gt, lt

  assign RAM_DIN = combined_DOUT;
  assign RAM_DIN_2 = combined_DOUT;

  // Notes on the sheet:
  //   Combines two read or write requests to a single one, if they hit the same address
  //   NOTE: Does not register anything!
  //   Edge Case:
  //   Do not output if BE is all 0
endmodule

module G32_MEMC_C_ByteLane (
  input  A_BE,
  input  B_BE,
  input  [7:0] A_DIN,
  input  [7:0] B_DIN,
  output combined_BE,
  output [7:0] combined_DOUT
);

  or or_1 (combined_BE, A_BE, B_BE);
  Multiplexer #(.width(8), .disabled(0), .enable("false")) multiplexer_1 (
    .in0(A_DIN), .in1(B_DIN), .out(combined_DOUT), .sel(B_BE));

  // Notes on the sheet:
  //   Current solution:
  //   Prioritize the later lane
  //   This handles what happens on a write conflict (meaning two lanes write to the same byte at the same time)
endmodule

module G32_THREAD (
  input  clk,
  input  reset,
  input  en,
  input  [2:0] predicate,
  input  [3:0] alu_cmd,
  input  ldr_ram,
  input  rf_wr,
  input  [4:0] rd,
  input  [1:0] tid,
  input  alu_is_lea,
  input  alu_sel_imm,
  input  [4:0] rb,
  input  [4:0] ra,
  input  [31:0] imm,
  input  [1:0] lane_id_in,
  input  LDS_STALL,
  input  RAM_STALL,
  input  [15:0] wg_x,
  input  [15:0] wg_y,
  input  [15:0] wg_x_2,
  input  [15:0] wg_y_2,
  input  [31:0] LDS_DIN,
  input  [31:0] RAM_DIN,
  input  [15:0] wg_x_n,
  input  [15:0] wg_y_n,
  input  [15:0] grid_x_n,
  input  [15:0] grid_y_n,
  input  [3:0] exec_mask,
  output [3:0] RAM_BE,
  output [3:0] LDS_BE,
  output LDS_STB,
  output RAM_STB,
  output [1:0] lane_id_out,
  output LDS_WR,
  output RAM_WR,
  output [9:0] LDS_ADDR,
  output [11:0] RAM_ADDR,
  output [31:0] LDS_DOUT,
  output [31:0] RAM_DOUT,
  output exec_mask_next
);

  wire g32_t_condcheck_1_active, g32_t_io_1_stall_rd, g32_t_io_1_stall_wr, g32_t_rf_bank_1_pred_active,
       pull_resistor_2_node, pull_resistor_3_node, register_10_q, register_13_q, register_14_q,
       register_17_q, register_18_q, register_22_q, register_23_q, register_24_q, s_r_ff_1_q;
  wire [1:0] register_1_q, register_16_q, register_26_q;
  wire [2:0] register_11_q;
  wire [3:0] register_12_q;
  wire [4:0] register_15_q, register_25_q;
  wire [9:0] RaRb_2_q;
  wire [15:0] register_2_q, register_3_q, register_4_q, register_5_q, register_6_q, register_7_q,
       register_8_q, register_9_q;
  wire [31:0] g32_t_alu_1_alu_out, g32_t_alu_ff_1_ra_3, g32_t_alu_ff_1_rb_3, g32_t_rf_bank_1_ra_2,
       g32_t_rf_bank_1_rb_2, register_19_q, register_20_q, register_21_q, register_27_q, register_28_q,
       undriven;

  Pull_Resistor pull_resistor_1 (.node(lane_id_in));
  Pull_Resistor pull_resistor_2 (.node(pull_resistor_2_node));
  G32_T_RF_Bank g32_t_rf_bank_1 (
    .clk(clk), .reset(reset), .wr(pull_resistor_3_node), .tid_wr(tid), .rd(register_28_q), .rb(rb), .ra(ra),
    .rd_2(register_25_q), .ra_2(g32_t_rf_bank_1_ra_2), .rb_2(g32_t_rf_bank_1_rb_2), .tid_rd(register_26_q),
    .predicate(predicate), .pred_active(g32_t_rf_bank_1_pred_active));
  Register #(.width(2)) register_1 (.D(lane_id_in), .Q(register_1_q), .clk(clk), .clr(reset));  // open: en
  Register #(.width(16)) register_2 (.D(wg_x), .Q(register_2_q), .clk(clk), .clr(reset));  // open: en
  Register #(.width(16)) register_3 (.D(wg_y), .Q(register_3_q), .clk(clk), .clr(reset));  // open: en
  Register #(.width(16)) register_4 (.D(wg_x_2), .Q(register_4_q), .clk(clk), .clr(reset));  // open: en
  Register #(.width(16)) register_5 (.D(wg_y_2), .Q(register_5_q), .clk(clk), .clr(reset));  // open: en
  Register #(.width(16)) register_6 (.D(wg_x_n), .Q(register_6_q), .clk(clk), .clr(reset));  // open: en
  Register #(.width(16)) register_7 (.D(wg_y_n), .Q(register_7_q), .clk(clk), .clr(reset));  // open: en
  Register #(.width(16)) register_8 (.D(grid_x_n), .Q(register_8_q), .clk(clk), .clr(reset));  // open: en
  Register #(.width(16)) register_9 (.D(grid_y_n), .Q(register_9_q), .clk(clk), .clr(reset));  // open: en
  LED Error (.in(s_r_ff_1_q));
  S_R_Flip_Flop s_r_ff_1 (
    .S(pull_resistor_2_node), .clk(clk), .Q(s_r_ff_1_q), .reset(reset));  // open: R, Qn, preset, en
  // Probe on imm
  Adder #(.width(2)) adder_1 (.a(lane_id_in), .b(2'b01), .out(lane_id_out));  // open: cin, cout
  // Probe on register_1_q
  // Probe on register_2_q
  // Probe on register_3_q
  // Probe on register_4_q
  // Probe on register_5_q
  // Probe on g32_t_rf_bank_1_ra_2
  // Probe on g32_t_rf_bank_1_rb_2
  Register #(.width(1)) register_10 (
    .D(g32_t_rf_bank_1_pred_active), .en(en), .Q(register_10_q), .clk(clk), .clr(reset));
  // Probe on register_10_q
  Register #(.width(3)) register_11 (.D(predicate), .en(en), .Q(register_11_q), .clk(clk), .clr(reset));
  // Probe on register_11_q
  Register #(.width(4)) register_12 (.D(alu_cmd), .en(en), .Q(register_12_q), .clk(clk), .clr(reset));
  // Probe on RaRb_2_q
  Register #(.width(10)) RaRb_2 (.D({rb, ra}), .en(en), .Q(RaRb_2_q), .clk(clk), .clr(reset));
  Register #(.width(1)) register_13 (.D(ldr_ram), .en(en), .Q(register_13_q), .clk(clk), .clr(reset));
  Register #(.width(1)) register_14 (.D(rf_wr), .en(en), .Q(register_14_q), .clk(clk), .clr(reset));
  Register #(.width(5)) register_15 (.D(rd), .en(en), .Q(register_15_q), .clk(clk), .clr(reset));
  Register #(.width(2)) register_16 (.D(tid), .en(en), .Q(register_16_q), .clk(clk), .clr(reset));
  Register #(.width(1)) register_17 (.D(alu_is_lea), .en(en), .Q(register_17_q), .clk(clk), .clr(reset));
  Register #(.width(1)) register_18 (.D(alu_sel_imm), .en(en), .Q(register_18_q), .clk(clk), .clr(reset));
  Register #(.width(32)) register_19 (.D(g32_t_rf_bank_1_ra_2), .en(en), .Q(register_19_q), .clk(clk), .clr(reset));
  Register #(.width(32)) register_20 (.D(g32_t_rf_bank_1_rb_2), .en(en), .Q(register_20_q), .clk(clk), .clr(reset));
  Register #(.width(32)) register_21 (.D(imm), .en(en), .Q(register_21_q), .clk(clk), .clr(reset));
  G32_T_CondCheck g32_t_condcheck_1 (
    .wb_dest(register_25_q), .pred_src(register_11_q), .pred_result(register_10_q),
    .active(g32_t_condcheck_1_active), .wb_d(register_28_q));
  // Probe on register_12_q
  // Probe on register_14_q
  // Probe on register_15_q
  // Probe on register_16_q
  // Probe on register_17_q
  // Probe on register_18_q
  G32_T_ALU_FF g32_t_alu_ff_1 (
    .ra(RaRb_2_q[4:0]), .ra_2(register_19_q), .rb(RaRb_2_q[9:5]), .rb_2(register_20_q),
    .rd_next(register_25_q), .rd_next_2(register_28_q), .ra_3(g32_t_alu_ff_1_ra_3), .rb_3(g32_t_alu_ff_1_rb_3));
  // Probe on register_21_q
  G32_T_ALU g32_t_alu_1 (
    .ra(g32_t_alu_ff_1_ra_3), .rb(g32_t_alu_ff_1_rb_3), .imm(register_21_q), .alu_out(g32_t_alu_1_alu_out),
    .alu_cmd(register_12_q), .alu_sel_imm(register_18_q), .alu_is_lea(register_17_q));
  // Probe on g32_t_condcheck_1_active
  // Probe on register_22_q
  Register #(.width(1)) register_22 (.D(g32_t_condcheck_1_active), .en(en), .Q(register_22_q), .clk(clk), .clr(reset));
  Register #(.width(1)) register_23 (.D(register_13_q), .en(en), .Q(register_23_q), .clk(clk), .clr(reset));
  Register #(.width(1)) register_24 (.D(register_14_q), .en(en), .Q(register_24_q), .clk(clk), .clr(reset));
  Register #(.width(5)) register_25 (.D(register_15_q), .en(en), .Q(register_25_q), .clk(clk), .clr(reset));
  Register #(.width(2)) register_26 (.D(register_16_q), .en(en), .Q(register_26_q), .clk(clk), .clr(reset));
  Register #(.width(32)) register_27 (.D(register_20_q), .en(en), .Q(register_27_q), .clk(clk), .clr(reset));
  Register #(.width(32)) register_28 (.D(g32_t_alu_1_alu_out), .en(en), .Q(register_28_q), .clk(clk), .clr(reset));
  // Probe on g32_t_alu_1_alu_out
  G32_T_IO g32_t_io_1 (
    .clk(clk), .reset(reset), .global_en(en), .en_rd(g32_t_condcheck_1_active), .en_wr(register_22_q),
    .ldr_ram_rd(register_13_q), .ldr_ram_wr(register_23_q), .addr_rd(undriven), .addr_wr(register_27_q),
    .alu_in(register_28_q), .stall_rd(g32_t_io_1_stall_rd), .stall_wr(g32_t_io_1_stall_wr),
    .LDS_STB(LDS_STB), .LDS_WR(LDS_WR), .LDS_ADDR(LDS_ADDR), .RAM_ADDR(RAM_ADDR), .LDS_STALL(LDS_STALL),
    .LDS_DIN(LDS_DIN), .LDS_DOUT(LDS_DOUT), .RAM_STB(RAM_STB), .RAM_WR(RAM_WR), .RAM_DOUT(RAM_DOUT),
    .RAM_STALL(RAM_STALL), .RAM_DIN(RAM_DIN));
  // Probe on register_24_q
  // Probe on register_25_q
  // Probe on register_26_q
  // Probe on register_27_q
  // Probe on register_28_q
  Pull_Resistor pull_resistor_3 (.node(pull_resistor_3_node));
  assign pull_resistor_3_node = register_22_q ? register_24_q : 1'bz;  // Controlled_Buffer controlled_buffer_1

  // Notes on the sheet:
  //   INSTRUCTION DECODE
  //   ADDRESSES ARE WRONG ->
  //   STALLS NOT HANDLED! ->
  //   EXECUTE / READ
  //   WRITEBACK / STORE
endmodule

module G32_T_RF_Bank (
  input  clk,
  input  reset,
  input  wr,
  input  [1:0] tid_rd,
  input  [1:0] tid_wr,
  input  [31:0] rd,
  input  [4:0] rb,
  input  [4:0] ra,
  input  [4:0] rd_2,
  input  [2:0] predicate,
  output pred_active,
  output [31:0] ra_2,
  output [31:0] rb_2
);

  wire decoder_1_out0, decoder_1_out1, decoder_1_out2, decoder_1_out3, g32_t_rf_1_pred_active,
       g32_t_rf_2_pred_active, g32_t_rf_3_pred_active, g32_t_rf_4_pred_active, g32_t_rf_ff_1_ff_d2a,
       g32_t_rf_ff_1_ff_d2b;
  wire [31:0] g32_t_rf_1_ra_2, g32_t_rf_1_rb_2, g32_t_rf_2_ra_2, g32_t_rf_2_rb_2, g32_t_rf_3_ra_2,
       g32_t_rf_3_rb_2, g32_t_rf_4_ra_2, g32_t_rf_4_rb_2, multiplexer_2_out, multiplexer_3_out;

  Decoder #(.select(2), .disabled(0)) decoder_1 (
    .out0(decoder_1_out0), .out1(decoder_1_out1), .out2(decoder_1_out2), .out3(decoder_1_out3), .sel(tid_wr),
    .en(wr));
  G32_T_RF_FF g32_t_rf_ff_1 (
    .wr(wr), .tid_rd(tid_rd), .tid_wr(tid_wr), .rb(rb), .ra(ra), .rd(rd_2), .ff_d2b(g32_t_rf_ff_1_ff_d2b),
    .ff_d2a(g32_t_rf_ff_1_ff_d2a));
  G32_T_RF g32_t_rf_1 (
    .clk(clk), .reset(reset), .wr(decoder_1_out0), .rd(rd), .rb(rb), .ra(ra), .rd_2(rd_2),
    .ra_2(g32_t_rf_1_ra_2), .rb_2(g32_t_rf_1_rb_2), .predicate(predicate),
    .pred_active(g32_t_rf_1_pred_active));
  G32_T_RF g32_t_rf_2 (
    .clk(clk), .reset(reset), .wr(decoder_1_out1), .rd(rd), .rb(rb), .ra(ra), .rd_2(rd_2),
    .ra_2(g32_t_rf_2_ra_2), .rb_2(g32_t_rf_2_rb_2), .predicate(predicate),
    .pred_active(g32_t_rf_2_pred_active));
  G32_T_RF g32_t_rf_3 (
    .clk(clk), .reset(reset), .wr(decoder_1_out2), .rd(rd), .rb(rb), .ra(ra), .rd_2(rd_2),
    .ra_2(g32_t_rf_3_ra_2), .rb_2(g32_t_rf_3_rb_2), .predicate(predicate),
    .pred_active(g32_t_rf_3_pred_active));
  G32_T_RF g32_t_rf_4 (
    .clk(clk), .reset(reset), .wr(decoder_1_out3), .rd(rd), .rb(rb), .ra(ra), .rd_2(rd_2),
    .ra_2(g32_t_rf_4_ra_2), .rb_2(g32_t_rf_4_rb_2), .predicate(predicate),
    .pred_active(g32_t_rf_4_pred_active));
  Multiplexer #(.select(2), .disabled(0), .enable("false")) multiplexer_1 (
    .in0(g32_t_rf_1_pred_active), .in1(g32_t_rf_2_pred_active), .in2(g32_t_rf_3_pred_active),
    .in3(g32_t_rf_4_pred_active), .out(pred_active), .sel(tid_rd));
  Multiplexer #(.select(2), .width(32), .disabled(0), .enable("false")) multiplexer_2 (
    .in0(g32_t_rf_1_ra_2), .in1(g32_t_rf_2_ra_2), .in2(g32_t_rf_3_ra_2), .in3(g32_t_rf_4_ra_2),
    .out(multiplexer_2_out), .sel(tid_rd));
  Multiplexer #(.select(2), .width(32), .disabled(0), .enable("false")) multiplexer_3 (
    .in0(g32_t_rf_1_rb_2), .in1(g32_t_rf_2_rb_2), .in2(g32_t_rf_3_rb_2), .in3(g32_t_rf_4_rb_2),
    .out(multiplexer_3_out), .sel(tid_rd));
  Multiplexer #(.width(32), .disabled(0), .enable("false")) multiplexer_4 (
    .in0(multiplexer_2_out), .in1(rd), .out(ra_2), .sel(g32_t_rf_ff_1_ff_d2b));
  Multiplexer #(.width(32), .disabled(0), .enable("false")) multiplexer_5 (
    .in0(multiplexer_3_out), .in1(rd), .out(rb_2), .sel(g32_t_rf_ff_1_ff_d2a));
endmodule

module G32_T_RF_FF (
  input  wr,
  input  [1:0] tid_rd,
  input  [1:0] tid_wr,
  input  [4:0] rb,
  input  [4:0] ra,
  input  [4:0] rd,
  output ff_d2b,
  output ff_d2a
);

  wire and_1_out, comparator_1_eq, comparator_2_eq, comparator_3_eq;

  Comparator #(.width(2)) comparator_1 (.a(tid_rd), .b(tid_wr), .eq(comparator_1_eq));  // open: gt, lt
  Comparator #(.width(5)) comparator_2 (.a(rb), .b(rd), .eq(comparator_2_eq));  // open: gt, lt
  Comparator #(.width(5)) comparator_3 (.a(ra), .b(rd), .eq(comparator_3_eq));  // open: gt, lt
  and and_1 (and_1_out, wr, comparator_1_eq);
  and and_2 (ff_d2b, and_1_out, comparator_2_eq);
  and and_3 (ff_d2a, and_1_out, comparator_3_eq);
endmodule

module G32_T_RF (
  input  clk,
  input  reset,
  input  wr,
  input  [2:0] predicate,
  input  [31:0] rd,
  input  [4:0] rb,
  input  [4:0] ra,
  input  [4:0] rd_2,
  output pred_active,
  output [31:0] ra_2,
  output [31:0] rb_2
);

  wire comparator_1_eq, decoder_1_out0, decoder_1_out1, decoder_1_out2, decoder_1_out3, decoder_1_out4,
       decoder_1_out5, decoder_1_out6, decoder_1_out7, decoder_1_out8, decoder_1_out9, decoder_1_out10,
       decoder_1_out11, decoder_1_out12, decoder_1_out13, decoder_1_out14, decoder_1_out15, decoder_1_out16,
       decoder_1_out17, decoder_1_out18, decoder_1_out19, decoder_1_out20, decoder_1_out21, decoder_1_out22,
       decoder_1_out23, decoder_1_out24, decoder_1_out25, decoder_1_out26, decoder_1_out27, decoder_1_out28,
       decoder_1_out29, decoder_1_out30, decoder_1_out31, pull_resistor_1_node;
  wire [31:0] multiplexer_1_out, pull_resistor_2_node, register_1_q, register_2_q, register_3_q,
       register_4_q, register_5_q, register_6_q, register_7_q, register_8_q, register_9_q, register_10_q,
       register_11_q, register_12_q, register_13_q, register_14_q, register_15_q, register_16_q,
       register_17_q, register_18_q, register_19_q, register_20_q, register_21_q, register_22_q,
       register_23_q, register_24_q, register_25_q, register_26_q, register_27_q, register_28_q,
       register_29_q, register_30_q, register_31_q, register_32_q;

  Decoder #(.select(5), .disabled(0)) decoder_1 (
    .out0(decoder_1_out0), .out1(decoder_1_out1), .out2(decoder_1_out2), .out3(decoder_1_out3),
    .out4(decoder_1_out4), .out5(decoder_1_out5), .out6(decoder_1_out6), .out7(decoder_1_out7),
    .out8(decoder_1_out8), .out9(decoder_1_out9), .out10(decoder_1_out10), .out11(decoder_1_out11),
    .out12(decoder_1_out12), .out13(decoder_1_out13), .out14(decoder_1_out14), .out15(decoder_1_out15),
    .out16(decoder_1_out16), .out17(decoder_1_out17), .out18(decoder_1_out18), .out19(decoder_1_out19),
    .out20(decoder_1_out20), .out21(decoder_1_out21), .out22(decoder_1_out22), .out23(decoder_1_out23),
    .out24(decoder_1_out24), .out25(decoder_1_out25), .out26(decoder_1_out26), .out27(decoder_1_out27),
    .out28(decoder_1_out28), .out29(decoder_1_out29), .out30(decoder_1_out30), .out31(decoder_1_out31),
    .sel(rd_2), .en(wr));
  Pull_Resistor pull_resistor_1 (.node(pull_resistor_1_node));
  Register #(.width(32)) register_1 (.D(rd), .en(pull_resistor_1_node), .Q(register_1_q), .clk(clk), .clr(reset));
  Register #(.width(32)) register_2 (.D(rd), .en(decoder_1_out1), .Q(register_2_q), .clk(clk), .clr(reset));
  Register #(.width(32)) register_3 (.D(rd), .en(decoder_1_out2), .Q(register_3_q), .clk(clk), .clr(reset));
  Register #(.width(32)) register_4 (.D(rd), .en(decoder_1_out3), .Q(register_4_q), .clk(clk), .clr(reset));
  Register #(.width(32)) register_5 (.D(rd), .en(decoder_1_out4), .Q(register_5_q), .clk(clk), .clr(reset));
  Register #(.width(32)) register_6 (.D(rd), .en(decoder_1_out5), .Q(register_6_q), .clk(clk), .clr(reset));
  Register #(.width(32)) register_7 (.D(rd), .en(decoder_1_out6), .Q(register_7_q), .clk(clk), .clr(reset));
  Register #(.width(32)) register_8 (.D(rd), .en(decoder_1_out7), .Q(register_8_q), .clk(clk), .clr(reset));
  Register #(.width(32)) register_9 (.D(rd), .en(decoder_1_out8), .Q(register_9_q), .clk(clk), .clr(reset));
  Register #(.width(32)) register_10 (.D(rd), .en(decoder_1_out9), .Q(register_10_q), .clk(clk), .clr(reset));
  Register #(.width(32)) register_11 (.D(rd), .en(decoder_1_out10), .Q(register_11_q), .clk(clk), .clr(reset));
  Register #(.width(32)) register_12 (.D(rd), .en(decoder_1_out11), .Q(register_12_q), .clk(clk), .clr(reset));
  Register #(.width(32)) register_13 (.D(rd), .en(decoder_1_out12), .Q(register_13_q), .clk(clk), .clr(reset));
  Register #(.width(32)) register_14 (.D(rd), .en(decoder_1_out13), .Q(register_14_q), .clk(clk), .clr(reset));
  Register #(.width(32)) register_15 (.D(rd), .en(decoder_1_out14), .Q(register_15_q), .clk(clk), .clr(reset));
  Register #(.width(32)) register_16 (.D(rd), .en(decoder_1_out15), .Q(register_16_q), .clk(clk), .clr(reset));
  Register #(.width(32)) register_17 (.D(rd), .en(decoder_1_out16), .Q(register_17_q), .clk(clk), .clr(reset));
  Register #(.width(32)) register_18 (.D(rd), .en(decoder_1_out17), .Q(register_18_q), .clk(clk), .clr(reset));
  Register #(.width(32)) register_19 (.D(rd), .en(decoder_1_out18), .Q(register_19_q), .clk(clk), .clr(reset));
  Register #(.width(32)) register_20 (.D(rd), .en(decoder_1_out19), .Q(register_20_q), .clk(clk), .clr(reset));
  Register #(.width(32)) register_21 (.D(rd), .en(decoder_1_out20), .Q(register_21_q), .clk(clk), .clr(reset));
  Register #(.width(32)) register_22 (.D(rd), .en(decoder_1_out21), .Q(register_22_q), .clk(clk), .clr(reset));
  Register #(.width(32)) register_23 (.D(rd), .en(decoder_1_out22), .Q(register_23_q), .clk(clk), .clr(reset));
  Register #(.width(32)) register_24 (.D(rd), .en(decoder_1_out23), .Q(register_24_q), .clk(clk), .clr(reset));
  Register #(.width(32)) register_25 (.D(rd), .en(decoder_1_out24), .Q(register_25_q), .clk(clk), .clr(reset));
  Register #(.width(32)) register_26 (.D(rd), .en(decoder_1_out25), .Q(register_26_q), .clk(clk), .clr(reset));
  Register #(.width(32)) register_27 (.D(rd), .en(decoder_1_out26), .Q(register_27_q), .clk(clk), .clr(reset));
  Register #(.width(32)) register_28 (.D(rd), .en(decoder_1_out27), .Q(register_28_q), .clk(clk), .clr(reset));
  Register #(.width(32)) register_29 (.D(rd), .en(decoder_1_out28), .Q(register_29_q), .clk(clk), .clr(reset));
  Register #(.width(32)) register_30 (.D(rd), .en(decoder_1_out29), .Q(register_30_q), .clk(clk), .clr(reset));
  Register #(.width(32)) register_31 (.D(rd), .en(decoder_1_out30), .Q(register_31_q), .clk(clk), .clr(reset));
  Register #(.width(32)) register_32 (.D(rd), .en(decoder_1_out31), .Q(register_32_q), .clk(clk), .clr(reset));
  Pull_Resistor pull_resistor_2 (.node(pull_resistor_2_node));
  Multiplexer #(.select(2), .width(32), .enable("false")) multiplexer_1 (
    .in0(register_1_q), .in1(register_3_q), .in2(register_4_q), .in3(register_5_q), .out(multiplexer_1_out),
    .sel(predicate[1:0]));
  Comparator #(.width(32)) comparator_1 (
    .a(pull_resistor_2_node), .b(multiplexer_1_out), .eq(comparator_1_eq));  // open: gt, lt
  xor xor_1 (pred_active, predicate[2], comparator_1_eq);
  Multiplexer #(.select(5), .width(32), .enable("false")) multiplexer_2 (
    .in0(register_1_q), .in1(register_2_q), .in2(register_3_q), .in3(register_4_q), .in4(register_5_q),
    .in5(register_6_q), .in6(register_7_q), .in7(register_8_q), .in8(register_9_q), .in9(register_10_q),
    .in10(register_11_q), .in11(register_12_q), .in12(register_13_q), .in13(register_14_q),
    .in14(register_15_q), .in15(register_16_q), .in16(register_17_q), .in17(register_18_q),
    .in18(register_19_q), .in19(register_20_q), .in20(register_21_q), .in21(register_22_q),
    .in22(register_23_q), .in23(register_24_q), .in24(register_25_q), .in25(register_26_q),
    .in26(register_27_q), .in27(register_28_q), .in28(register_29_q), .in29(register_30_q),
    .in30(register_31_q), .in31(register_32_q), .out(rb_2), .sel(rb));
  Multiplexer #(.select(5), .width(32), .enable("false")) multiplexer_3 (
    .in0(register_1_q), .in1(register_2_q), .in2(register_3_q), .in3(register_4_q), .in4(register_5_q),
    .in5(register_6_q), .in6(register_7_q), .in7(register_8_q), .in8(register_9_q), .in9(register_10_q),
    .in10(register_11_q), .in11(register_12_q), .in12(register_13_q), .in13(register_14_q),
    .in14(register_15_q), .in15(register_16_q), .in16(register_17_q), .in17(register_18_q),
    .in18(register_19_q), .in19(register_20_q), .in20(register_21_q), .in21(register_22_q),
    .in22(register_23_q), .in23(register_24_q), .in24(register_25_q), .in25(register_26_q),
    .in26(register_27_q), .in27(register_28_q), .in28(register_29_q), .in29(register_30_q),
    .in30(register_31_q), .in31(register_32_q), .out(ra_2), .sel(ra));
endmodule

module G32_T_ALU (
  input  alu_is_lea,
  input  [3:0] alu_cmd,
  input  alu_sel_imm,
  input  [31:0] ra,
  input  [31:0] rb,
  input  [31:0] imm,
  output [31:0] alu_out
);

  wire adder_1_cout;
  wire [31:0] adder_1_out, adder_2_out, and_1_out, divider_1_out, multiplexer_1_out, multiplier_1_out,
       or_1_out, pull_resistor_1_node, pull_resistor_2_node, pull_resistor_3_node, pull_resistor_4_node,
       pull_resistor_5_node, pull_resistor_6_node, pull_resistor_7_node, pull_resistor_8_node, shifter_1_out,
       shifter_2_out, shifter_3_out, subtractor_1_out, xor_1_out;

  Multiplexer #(.width(32), .disabled(0), .enable("false")) multiplexer_1 (
    .in0(rb), .in1(imm), .out(multiplexer_1_out), .sel(alu_sel_imm));
  Adder #(.width(32)) adder_1 (.out(adder_1_out), .cout(adder_1_cout));  // open: a, b, cin
  Pull_Resistor #(.pull(1)) pull_resistor_1 (.node(pull_resistor_1_node));
  BitFinder bitfinder_1 ();  // open: in, index, found
  Multiplexer #(.width(32), .disabled(0), .enable("false")) multiplexer_2 (
    .in0(adder_1_out), .in1(pull_resistor_1_node), .sel(adder_1_cout));  // open: out
  Pull_Resistor pull_resistor_2 (.node(pull_resistor_2_node));
  Comparator #(.width(32)) comparator_1 (.a(pull_resistor_2_node));  // open: b, gt, eq, lt
  Adder #(.width(32)) adder_2 (.a(ra), .b(multiplexer_1_out), .out(adder_2_out));  // open: cin, cout
  Multiplier #(.width(32)) multiplier_1 (.a(ra), .b(multiplexer_1_out), .out(multiplier_1_out));  // open: cin, cout
  Pull_Resistor #(.pull("X")) pull_resistor_3 (.node(pull_resistor_3_node));
  assign and_1_out = ra & multiplexer_1_out;  // AND_Gate and_1, 32 bits wide
  assign or_1_out = ra | multiplexer_1_out;  // OR_Gate or_1, 32 bits wide
  Shifter #(.width(32)) shifter_1 (.in(ra), .\dist (multiplexer_1_out[4:0]), .out(shifter_1_out));
  Shifter #(.width(32), .shift("lr")) shifter_2 (.in(ra), .\dist (multiplexer_1_out[4:0]), .out(shifter_2_out));
  Shifter #(.width(32), .shift("ar")) shifter_3 (.in(ra), .\dist (multiplexer_1_out[4:0]), .out(shifter_3_out));
  Subtractor #(.width(32)) subtractor_1 (.a(ra), .b(multiplexer_1_out), .out(subtractor_1_out));  // open: bin, bout
  Divider #(.width(32)) divider_1 (.a(ra), .b(multiplexer_1_out), .out(divider_1_out));  // open: upper, rem
  Pull_Resistor #(.pull("X")) pull_resistor_4 (.node(pull_resistor_4_node));
  assign xor_1_out = ra ^ multiplexer_1_out;  // XOR_Gate xor_1, 32 bits wide
  Pull_Resistor #(.pull("X")) pull_resistor_5 (.node(pull_resistor_5_node));
  Pull_Resistor #(.pull("X")) pull_resistor_6 (.node(pull_resistor_6_node));
  Pull_Resistor #(.pull("X")) pull_resistor_7 (.node(pull_resistor_7_node));
  Pull_Resistor #(.pull("X")) pull_resistor_8 (.node(pull_resistor_8_node));
  Multiplexer #(.select(4), .width(32), .enable("false")) multiplexer_3 (
    .in0(adder_2_out), .in1(multiplier_1_out), .in2(pull_resistor_3_node), .in3(and_1_out), .in4(or_1_out),
    .in5(shifter_1_out), .in6(shifter_2_out), .in7(shifter_3_out), .in8(subtractor_1_out),
    .in9(divider_1_out), .in10(pull_resistor_4_node), .in11(xor_1_out), .in12(pull_resistor_5_node),
    .in13(pull_resistor_6_node), .in14(pull_resistor_7_node), .in15(pull_resistor_8_node), .out(alu_out),
    .sel(alu_cmd));
endmodule

module G32_T_ALU_FF (
  input  [4:0] ra,
  input  [31:0] ra_2,
  input  [4:0] rb,
  input  [31:0] rb_2,
  input  [4:0] rd_next,
  input  [31:0] rd_next_2,
  output [31:0] ra_3,
  output [31:0] rb_3
);

  wire comparator_1_eq, comparator_2_eq;

  Comparator #(.width(5)) comparator_1 (.a(ra), .b(rd_next), .eq(comparator_1_eq));  // open: gt, lt
  Multiplexer #(.width(32), .disabled(0), .enable("false")) multiplexer_1 (
    .in0(ra_2), .in1(rd_next_2), .out(ra_3), .sel(comparator_1_eq));
  Comparator #(.width(5)) comparator_2 (.a(rb), .b(rd_next), .eq(comparator_2_eq));  // open: gt, lt
  Multiplexer #(.width(32), .disabled(0), .enable("false")) multiplexer_2 (
    .in0(rb_2), .in1(rd_next_2), .out(rb_3), .sel(comparator_2_eq));
endmodule

module G32_T_CondCheck (
  input  [2:0] pred_src,
  input  [4:0] wb_dest,
  input  pred_result,
  input  [31:0] wb_d,
  output active
);

  wire and_1_out, comparator_1_eq, comparator_2_eq, comparator_3_eq, xor_1_out;
  wire [1:0] pull_resistor_1_node;
  wire [31:0] pull_resistor_2_node;

  Comparator #(.width(2)) comparator_1 (.a(pred_src[1:0]), .b(wb_dest[1:0]), .eq(comparator_1_eq));  // open: gt, lt
  Comparator #(.width(2)) comparator_2 (
    .a(wb_dest[4:3]), .b(pull_resistor_1_node), .eq(comparator_2_eq));  // open: gt, lt
  Pull_Resistor pull_resistor_1 (.node(pull_resistor_1_node));
  Comparator #(.width(32)) comparator_3 (.a(wb_d), .b(pull_resistor_2_node), .eq(comparator_3_eq));  // open: gt, lt
  Pull_Resistor pull_resistor_2 (.node(pull_resistor_2_node));
  and and_1 (and_1_out, comparator_1_eq, comparator_2_eq);
  xor xor_1 (xor_1_out, wb_dest[2], comparator_3_eq);
  Multiplexer #(.disabled(0), .enable("false")) multiplexer_1 (
    .in0(pred_result), .in1(xor_1_out), .out(active), .sel(and_1_out));
endmodule

module G32_T_Flags (
  input  clk,
  input  reset,
  input  en,
  input  [2:0] flag_update_mask,
  input  [2:0] condition,
  output [2:0] condition_2
);

  wire [2:0] controlled_buffer_1_out;

  assign controlled_buffer_1_out = en ? flag_update_mask : 3'bz;  // Controlled_Buffer controlled_buffer_1
  Pull_Resistor pull_resistor_1 (.node(controlled_buffer_1_out));
  Register #(.width(1)) register_1 (
    .D(condition[0]), .en(controlled_buffer_1_out[0]), .Q(condition_2[0]), .clk(clk), .clr(reset));
  Register #(.width(1)) register_2 (
    .D(condition[1]), .en(controlled_buffer_1_out[1]), .Q(condition_2[1]), .clk(clk), .clr(reset));
  Register #(.width(1)) register_3 (
    .D(condition[2]), .en(controlled_buffer_1_out[2]), .Q(condition_2[2]), .clk(clk), .clr(reset));
endmodule

module G32_T_IO (
  input  clk,
  input  reset,
  input  global_en,
  input  en_rd,
  input  en_wr,
  input  LDS_STB,
  input  ldr_ram_rd,
  input  LDS_WR,
  input  ldr_ram_wr,
  input  [31:0] addr_rd,
  input  [9:0] LDS_ADDR,
  input  [11:0] RAM_ADDR,
  input  [31:0] addr_wr,
  input  [31:0] LDS_DOUT,
  input  RAM_STB,
  input  [31:0] alu_in,
  input  RAM_WR,
  input  [31:0] RAM_DOUT,
  input  [31:0] RAM_DIN,
  output stall_rd,
  output stall_wr,
  output LDS_STALL,
  output [31:0] LDS_DIN,
  output RAM_STALL
);

  wire and_1_out, not_1_out, or_1_out, or_2_out;
  wire [11:0] demultiplexer_1_out0, demultiplexer_1_out1, demultiplexer_2_out0, demultiplexer_2_out1;

  and and_1 (and_1_out, global_en, or_1_out);
  or or_1 (or_1_out, en_rd, en_wr);
  Demultiplexer #(.width(12), .disabled(0), .enable("false")) demultiplexer_1 (
    .out0(demultiplexer_1_out0), .out1(demultiplexer_1_out1), .in(addr_rd[11:0]), .sel(ldr_ram_rd));
  Demultiplexer #(.width(12), .disabled(0), .enable("false")) demultiplexer_2 (
    .out0(demultiplexer_2_out0), .out1(demultiplexer_2_out1), .in(addr_wr[11:0]), .sel(ldr_ram_wr));
  or or_2 (or_2_out, and_1_out, en_wr);
  not not_1 (not_1_out, ldr_ram_rd);
  and and_2 (LDS_STB, or_2_out, not_1_out);
  and and_3 (RAM_STB, or_2_out, ldr_ram_rd);
  Pull_Resistor pull_resistor_1 ();  // open: node
  Controlled_Buffer #(.width(32)) controlled_buffer_1 ();  // open: in, out, en
  Pull_Resistor #(.pull("X")) pull_resistor_2 (.node(stall_rd));
  Pull_Resistor #(.pull("X")) pull_resistor_3 (.node(stall_wr));

  assign LDS_DOUT = alu_in;
  assign LDS_WR = en_wr;
  assign RAM_ADDR[9:0] = LDS_ADDR;
  assign RAM_DOUT = alu_in;
  assign RAM_WR = en_wr;
endmodule

module G32_Controller (
  input  clk,
  input  reset,
  input  en,
  input  [15:0] wg_x_n,
  input  [15:0] wg_y_n,
  input  [15:0] grid_x_n,
  input  [15:0] grid_y_n,
  input  [3:0] exec_mask_in,
  input  [3:0] halt_mask_in,
  input  start,
  output reset_2,
  output [1:0] hyperthread_id,
  output [3:0] exec_mask_out,
  output [15:0] wg_x_n_2,
  output [15:0] wg_y_n_2,
  output [15:0] grid_x_n_2,
  output [15:0] grid_y_n_2,
  output [15:0] wg_x,
  output [15:0] wg_y,
  output [15:0] grid_x,
  output [15:0] grid_y
);

  wire g32_ctrl_fsm_1_is_done, g32_ctrl_fsm_1_is_idle, g32_ctrl_fsm_1_is_running,
       g32_ctrl_fsm_1_is_setup_next_wg, g32_ctrl_invocationhandling_1_done,
       g32_ctrl_invocationhandling_1_next_wg, pull_resistor_2_node;
  wire [3:0] pull_resistor_1_node;

  Pull_Resistor #(.pull(1)) pull_resistor_1 (.node(pull_resistor_1_node));
  G32_Ctrl_Reset g32_ctrl_reset_1 (
    .clk(clk), .reset(reset), .en(en), .reset_2(g32_ctrl_invocationhandling_1_next_wg), .reset_3(reset_2));
  G32_Ctrl_ConfigRegs g32_ctrl_configregs_1 (
    .clk(clk), .reset(reset), .en(en), .is_in_idle(pull_resistor_2_node), .wg_x_n_2(wg_x_n_2),
    .wg_y_n_2(wg_y_n_2), .grid_x_n_2(grid_x_n_2), .grid_y_n_2(grid_y_n_2), .wg_x_n(wg_x_n), .wg_y_n(wg_y_n),
    .grid_x_n(grid_x_n), .grid_y_n(grid_y_n));
  Pull_Resistor #(.pull(1)) pull_resistor_2 (.node(pull_resistor_2_node));
  G32_Ctrl_FSM g32_ctrl_fsm_1 (
    .clk(clk), .reset(reset), .en(en), .start(start), .next_wg(g32_ctrl_invocationhandling_1_next_wg),
    .wg_done(g32_ctrl_invocationhandling_1_done), .is_idle(g32_ctrl_fsm_1_is_idle),
    .is_running(g32_ctrl_fsm_1_is_running), .is_setup_next_wg(g32_ctrl_fsm_1_is_setup_next_wg),
    .is_done(g32_ctrl_fsm_1_is_done));
  G32_Ctrl_InvocationHandling g32_ctrl_invocationhandling_1 (
    .clk(clk), .reset(reset), .en(en), .is_active(g32_ctrl_fsm_1_is_running), .wg_x_n(wg_x_n_2),
    .wg_y_n(wg_y_n_2), .grid_x_n(grid_x_n_2), .grid_y_n(grid_y_n_2), .wg_x(wg_x), .wg_y(wg_y),
    .grid_x(grid_x), .grid_y(grid_y), .halt_mask_in(halt_mask_in), .lane_mask_max(pull_resistor_1_node),
    .next_wg(g32_ctrl_invocationhandling_1_next_wg), .done(g32_ctrl_invocationhandling_1_done),
    .reset_lanes(reset_2), .exec_mask_in(exec_mask_in), .exec_mask_out(exec_mask_out));
  LED idle (.in(g32_ctrl_fsm_1_is_idle));
  LED running (.in(g32_ctrl_fsm_1_is_running));
  LED wg_done (.in(g32_ctrl_fsm_1_is_setup_next_wg));
  LED done (.in(g32_ctrl_fsm_1_is_done));

  assign hyperthread_id = 2'b00;

  // Notes on the sheet:
  //   en: pull=up
  //   start: pull=up
  //   later wait until everything is initialized
  //   For now always assume all lanes are started
  //   For now do not require the controller to enable the lanes
  //   TODO:
  //   This thing
  //   Update ID, ALU
  //   TODO:
  //   WE DO NOT YET SUPPORT HYPERTHREADING
  //   Add config registers to start a grid
  //   Divergence handling :(
  //   (in the scheduler)
  //   -> Do not allow modification of those if ctrl state != idle
endmodule

module G32_Ctrl_Reset (
  input  clk,
  input  reset,
  input  en,
  input  reset_2,
  output reset_3
);

  wire and_1_out, register_1_q;

  and and_1 (and_1_out, ~reset_2, register_1_q);  // AND_Gate
  S_R_Flip_Flop s_r_ff_1 (
    .S(reset_2), .clk(clk), .R(and_1_out), .Q(reset_3), .preset(reset), .en(en));  // open: Qn, reset
  Register #(.width(1)) register_1 (.D(reset_3), .Q(register_1_q), .clk(clk));  // open: en, clr

  // Notes on the sheet:
  //   en: pull=up
endmodule

module G32_Ctrl_ConfigRegs (
  input  clk,
  input  reset,
  input  en,
  input  is_in_idle,
  input  [15:0] wg_x_n,
  input  [15:0] wg_y_n,
  input  [15:0] grid_x_n,
  input  [15:0] grid_y_n,
  output [15:0] wg_x_n_2,
  output [15:0] wg_y_n_2,
  output [15:0] grid_x_n_2,
  output [15:0] grid_y_n_2
);

  wire and_1_out;

  and and_1 (and_1_out, is_in_idle, en);
  Register #(.width(16)) register_1 (.D(wg_x_n), .en(and_1_out), .Q(wg_x_n_2), .clk(clk), .clr(reset));
  Register #(.width(16)) register_2 (.D(wg_y_n), .en(and_1_out), .Q(wg_y_n_2), .clk(clk), .clr(reset));
  Register #(.width(16)) register_3 (.D(grid_x_n), .en(and_1_out), .Q(grid_x_n_2), .clk(clk), .clr(reset));
  Register #(.width(16)) register_4 (.D(grid_y_n), .en(and_1_out), .Q(grid_y_n_2), .clk(clk), .clr(reset));

  // Notes on the sheet:
  //   is_in_idle: pull=up
  //   en: pull=up
  //   Real config regs must also inform user of limits:
  //   grid, wg single dim limit is 2^16
endmodule

module G32_Ctrl_InvocationHandling (
  input  clk,
  input  reset,
  input  en,
  input  reset_lanes,
  input  [3:0] exec_mask_in,
  input  is_active,
  input  [3:0] lane_mask_max,
  input  [3:0] halt_mask_in,
  input  [15:0] wg_x_n,
  input  [15:0] wg_y_n,
  input  [15:0] grid_x_n,
  input  [15:0] grid_y_n,
  output [3:0] exec_mask_out,
  output next_wg,
  output done,
  output [15:0] wg_x,
  output [15:0] wg_y,
  output [15:0] grid_x,
  output [15:0] grid_y
);

  wire and_1_out, comparator_1_eq, g32_ctrl_ih_counter_1_done, pull_resistor_2_node, register_1_q;
  wire [3:0] multiplexer_1_out, pull_resistor_1_node, xnor_1_out;

  assign xnor_1_out = ~(lane_mask_max ^ halt_mask_in);  // XNOR_Gate xnor_1, 4 bits wide
  // Probe on comparator_1_eq
  Comparator #(.width(4)) comparator_1 (.a(xnor_1_out), .b(4'b1111), .eq(comparator_1_eq));  // open: gt, lt
  Multiplexer #(.width(4), .disabled(0), .enable("false")) multiplexer_1 (
    .in0(exec_mask_in), .in1(pull_resistor_1_node), .out(multiplexer_1_out), .sel(reset_lanes));
  Pull_Resistor #(.pull(1)) pull_resistor_1 (.node(pull_resistor_1_node));
  and and_1 (and_1_out, en, pull_resistor_2_node);
  Pull_Resistor #(.pull(1)) pull_resistor_2 (.node(pull_resistor_2_node));
  Register #(.width(1)) register_1 (.D(comparator_1_eq), .en(en), .Q(register_1_q), .clk(clk), .clr(reset));
  Register #(.width(4)) register_2 (.en(en), .clk(clk), .clr(reset));  // open: D, Q
  G32_Ctrl_IH_Counter g32_ctrl_ih_counter_1 (
    .en(en), .clk(clk), .reset(reset_lanes), .is_prev_wg_done(comparator_1_eq), .wg_limit(wg_x_n),
    .wg_x(wg_x), .done(g32_ctrl_ih_counter_1_done));
  G32_Ctrl_IH_Counter g32_ctrl_ih_counter_2 (
    .en(en), .clk(clk), .reset(reset_lanes), .is_prev_wg_done(g32_ctrl_ih_counter_1_done), .wg_limit(wg_y_n),
    .wg_x(wg_y), .done(done));
  Register #(.width(4)) register_3 (.D(multiplexer_1_out), .en(and_1_out), .Q(exec_mask_out), .clk(clk), .clr(reset));
  and and_2 (next_wg, register_1_q, ~done);  // AND_Gate
  Pull_Resistor pull_resistor_3 (.node(grid_x));
  Pull_Resistor pull_resistor_4 (.node(grid_y));

  // Notes on the sheet:
  //   reset_lanes: pull=up
  //   is_active: pull=up
  //   en: pull=up
  //   Registered inputs
  //   WE DO NOT YET SUPPORT GRIDs
  //   @ Startup enable all lanes
  //   TODO:
  //   Do not yet handle execution mask
  //   Keep it simple to test non divergent kernels
endmodule

module G32_Ctrl_IH_Counter (
  input  en,
  input  clk,
  input  reset,
  input  is_prev_wg_done,
  input  [15:0] wg_limit,
  output [15:0] wg_x,
  output done
);

  wire and_1_out, and_2_out, comparator_1_eq, comparator_2_eq, or_1_out, undriven, undriven_2, undriven_3;
  wire [15:0] adder_1_out, multiplexer_1_out, pull_resistor_1_node, pull_resistor_2_node;

  Multiplexer #(.width(16), .disabled(0), .enable("false")) multiplexer_1 (
    .in0(adder_1_out), .in1(pull_resistor_1_node), .out(multiplexer_1_out), .sel(comparator_1_eq));
  Pull_Resistor pull_resistor_1 (.node(pull_resistor_1_node));
  and and_1 (and_1_out, is_prev_wg_done, en);
  Register #(.width(16)) register_1 (.D(multiplexer_1_out), .en(and_1_out), .Q(wg_x), .clk(clk), .clr(reset));
  // Probe on wg_x
  // Probe on adder_1_out
  // Probe on comparator_1_eq
  Adder #(.width(16)) adder_1 (.a(wg_x), .b(16'h1), .out(adder_1_out));  // open: cin, cout
  Pull_Resistor pull_resistor_2 (.node(pull_resistor_2_node));
  Comparator #(.width(16)) comparator_1 (.a(adder_1_out), .b(wg_limit), .eq(comparator_1_eq));  // open: gt, lt
  Comparator #(.width(16)) comparator_2 (.a(wg_limit), .b(pull_resistor_2_node), .eq(comparator_2_eq));  // open: gt, lt
  and and_2 (and_2_out, comparator_2_eq, is_prev_wg_done);
  or or_1 (or_1_out, comparator_1_eq, and_2_out);
  Register #(.width(1)) register_2 (.D(or_1_out), .en(undriven_3), .Q(done), .clk(undriven_2), .clr(undriven));

  // Notes on the sheet:
  //   en: pull=up
  //   Handles SW bugs that declare wg_limit 0, we just handle it as a 1
endmodule

module G32_Ctrl_FSM (
  input  clk,
  input  reset,
  input  en,
  input  start,
  input  next_wg,
  input  wg_done,
  output is_idle,
  output is_running,
  output is_setup_next_wg,
  output is_done
);

  wire and_1_out, and_2_out, and_3_out, or_1_out;

  S_R_Flip_Flop s_r_ff_1 (.S(is_done), .clk(clk), .Q(is_idle), .reset(reset), .en(en));  // open: R, Qn, preset
  S_R_Flip_Flop s_r_ff_2 (.S(or_1_out), .clk(clk), .Q(is_running), .reset(reset), .en(en));  // open: R, Qn, preset
  S_R_Flip_Flop s_r_ff_3 (
    .S(and_2_out), .clk(clk), .Q(is_setup_next_wg), .reset(reset), .en(en));  // open: R, Qn, preset
  S_R_Flip_Flop s_r_ff_4 (.S(and_3_out), .clk(clk), .Q(is_done), .reset(reset), .en(en));  // open: R, Qn, preset
  // Probe on is_idle
  // Probe on is_running
  // Probe on is_setup_next_wg
  // Probe on is_done
  and and_1 (and_1_out, is_idle, start);
  and and_2 (and_2_out, is_running, next_wg);
  or or_1 (or_1_out, and_1_out, is_setup_next_wg);
  and and_3 (and_3_out, is_running, wg_done);

  // Notes on the sheet:
  //   en: pull=up
  //   wg_done: pull=up
  //   start: pull=up
  //   next_wg: pull=up
  //   FSM
  //   We do net yet support hyperthreading, so it's simple :)
endmodule

module FrameBuffer (
  input  clk,
  input  reset,
  input  en,
  input  RAM_STB,
  input  RAM_WR,
  input  [11:0] RAM_ADDR,
  input  [31:0] RAM_DIN,
  input  [6:0] FB_Addr_Page,
  output [31:0] Col0,
  output [31:0] Col1,
  output [6:0] FB_Addr_Page_2,
  output [31:0] Col2,
  output [31:0] Col3,
  output [31:0] Col4,
  output [31:0] Col5,
  output [31:0] Col6,
  output [31:0] Col7,
  output [31:0] Col0_2,
  output [31:0] Col1_2,
  output [31:0] Col2_2,
  output [31:0] Col3_2,
  output [31:0] Col4_2,
  output [31:0] Col5_2,
  output [31:0] Col6_2,
  output [31:0] Col7_2,
  output [31:0] Col0_3,
  output [31:0] Col1_3,
  output [31:0] Col2_3,
  output [31:0] Col3_3,
  output [31:0] Col4_3,
  output [31:0] Col5_3,
  output [31:0] Col6_3,
  output [31:0] Col7_3,
  output [31:0] Col0_4,
  output [31:0] Col1_4,
  output [31:0] Col2_4,
  output [31:0] Col3_4,
  output [31:0] Col4_4,
  output [31:0] Col5_4,
  output [31:0] Col6_4,
  output [31:0] Col7_4
);

  wire and_1_out, comparator_1_eq, decoder_1_out0, decoder_1_out1, decoder_1_out2, decoder_1_out3;

  Pull_Resistor pull_resistor_1 (.node(reset));
  Pull_Resistor #(.pull(1)) pull_resistor_2 (.node(en));
  Pull_Resistor #(.pull(1)) pull_resistor_3 (.node(RAM_STB));
  Pull_Resistor #(.pull(1)) pull_resistor_4 (.node(RAM_WR));
  Pull_Resistor pull_resistor_5 (.node(FB_Addr_Page));
  Comparator #(.width(7)) comparator_1 (.a(RAM_ADDR[11:5]), .b(FB_Addr_Page), .eq(comparator_1_eq));  // open: gt, lt
  Adder #(.width(7)) adder_1 (.a(FB_Addr_Page), .b(7'b0000001), .out(FB_Addr_Page_2));  // open: cin, cout
  and and_1 (and_1_out, en, comparator_1_eq);
  Decoder #(.select(2), .disabled(0)) decoder_1 (
    .out0(decoder_1_out0), .out1(decoder_1_out1), .out2(decoder_1_out2), .out3(decoder_1_out3),
    .sel(RAM_ADDR[4:3]), .en(and_1_out));
  FrameBuffer_Reg8 framebuffer_reg8_1 (
    .clk(clk), .reset(reset), .en(decoder_1_out0), .RAM_STB(RAM_STB), .RAM_WR(RAM_WR),
    .RAM_ADDR(RAM_ADDR[2:0]), .RAM_DIN(RAM_DIN), .Col0(Col0), .Col1(Col1), .Col3(Col3), .Col4(Col4),
    .Col5(Col5), .Col6(Col6), .Col7(Col7), .Col2(Col2));
  FrameBuffer_Reg8 framebuffer_reg8_2 (
    .clk(clk), .reset(reset), .en(decoder_1_out1), .RAM_STB(RAM_STB), .RAM_WR(RAM_WR),
    .RAM_ADDR(RAM_ADDR[2:0]), .RAM_DIN(RAM_DIN), .Col0(Col0_2), .Col1(Col1_2), .Col3(Col3_2), .Col4(Col4_2),
    .Col5(Col5_2), .Col6(Col6_2), .Col7(Col7_2), .Col2(Col2_2));
  FrameBuffer_Reg8 framebuffer_reg8_3 (
    .clk(clk), .reset(reset), .en(decoder_1_out2), .RAM_STB(RAM_STB), .RAM_WR(RAM_WR),
    .RAM_ADDR(RAM_ADDR[2:0]), .RAM_DIN(RAM_DIN), .Col0(Col0_3), .Col1(Col1_3), .Col3(Col3_3), .Col4(Col4_3),
    .Col5(Col5_3), .Col6(Col6_3), .Col7(Col7_3), .Col2(Col2_3));
  FrameBuffer_Reg8 framebuffer_reg8_4 (
    .clk(clk), .reset(reset), .en(decoder_1_out3), .RAM_STB(RAM_STB), .RAM_WR(RAM_WR),
    .RAM_ADDR(RAM_ADDR[2:0]), .RAM_DIN(RAM_DIN), .Col0(Col0_4), .Col1(Col1_4), .Col3(Col3_4), .Col4(Col4_4),
    .Col5(Col5_4), .Col6(Col6_4), .Col7(Col7_4), .Col2(Col2_4));

  // Notes on the sheet:
  //   en: pull=up
endmodule

module FrameBuffer_Reg8 (
  input  clk,
  input  reset,
  input  en,
  input  RAM_STB,
  input  RAM_WR,
  input  [2:0] RAM_ADDR,
  input  [31:0] RAM_DIN,
  output [31:0] Col0,
  output [31:0] Col1,
  output [31:0] Col2,
  output [31:0] Col3,
  output [31:0] Col4,
  output [31:0] Col5,
  output [31:0] Col6,
  output [31:0] Col7
);

  wire and_1_out, decoder_1_out0, decoder_1_out1, decoder_1_out2, decoder_1_out3, decoder_1_out4,
       decoder_1_out5, decoder_1_out6, decoder_1_out7;

  and and_1 (and_1_out, RAM_WR, RAM_STB, en);
  Decoder #(.select(3), .disabled(0)) decoder_1 (
    .out0(decoder_1_out0), .out1(decoder_1_out1), .out2(decoder_1_out2), .out3(decoder_1_out3),
    .out4(decoder_1_out4), .out5(decoder_1_out5), .out6(decoder_1_out6), .out7(decoder_1_out7),
    .sel(RAM_ADDR), .en(and_1_out));
  Register #(.width(32)) register_1 (.D(RAM_DIN), .en(decoder_1_out0), .Q(Col0), .clk(clk), .clr(reset));
  Register #(.width(32)) register_2 (.D(RAM_DIN), .en(decoder_1_out1), .Q(Col1), .clk(clk), .clr(reset));
  Register #(.width(32)) register_3 (.D(RAM_DIN), .en(decoder_1_out2), .Q(Col2), .clk(clk), .clr(reset));
  Register #(.width(32)) register_4 (.D(RAM_DIN), .en(decoder_1_out3), .Q(Col3), .clk(clk), .clr(reset));
  Register #(.width(32)) register_5 (.D(RAM_DIN), .en(decoder_1_out4), .Q(Col4), .clk(clk), .clr(reset));
  Register #(.width(32)) register_6 (.D(RAM_DIN), .en(decoder_1_out5), .Q(Col5), .clk(clk), .clr(reset));
  Register #(.width(32)) register_7 (.D(RAM_DIN), .en(decoder_1_out6), .Q(Col6), .clk(clk), .clr(reset));
  Register #(.width(32)) register_8 (.D(RAM_DIN), .en(decoder_1_out7), .Q(Col7), .clk(clk), .clr(reset));
  DotMatrix #(.matrixcols(32)) dotmatrix_1 ();  // open: col0, col1, col2, col3, col4, col5, col6, col7, col8, col9, col10, col11, col12, col13, col14, col15, col16, col17, col18, col19, col20, col21, col22, col23, col24, col25, col26, col27, col28, col29, col30, col31

  // Notes on the sheet:
  //   en: pull=up
endmodule

module Memory_BE (
  input  clk,
  input  reset,
  input  en,
  input  RAM_STB,
  input  RAM_WR,
  input  [3:0] RAM_BE,
  input  [15:0] RAM_ADDR,
  input  [31:0] RAM_DOUT,
  output RAM_ACK,
  output [31:0] RAM_DIN
);

  wire and_1_out, and_2_out;

  and and_1 (and_1_out, ~RAM_WR, en);  // AND_Gate
  and and_2 (and_2_out, RAM_WR, en);
  Register #(.width(1)) register_1 (.D(RAM_STB), .en(en), .Q(RAM_ACK), .clk(clk), .clr(reset));
  RAM #(.addrWidth(16), .bus("separate")) ram_1 (
    .addr(RAM_ADDR), .din(RAM_DOUT[7:0]), .data(RAM_DIN[7:0]), .str(and_2_out), .sel(RAM_BE[0]), .clk(clk),
    .ld(and_1_out), .clr(reset));
  RAM #(.addrWidth(16), .bus("separate")) ram_2 (
    .addr(RAM_ADDR), .din(RAM_DOUT[15:8]), .data(RAM_DIN[15:8]), .str(and_2_out), .sel(RAM_BE[1]), .clk(clk),
    .ld(and_1_out), .clr(reset));
  RAM #(.addrWidth(16), .bus("separate")) ram_3 (
    .addr(RAM_ADDR), .din(RAM_DOUT[23:16]), .data(RAM_DIN[23:16]), .str(and_2_out), .sel(RAM_BE[2]),
    .clk(clk), .ld(and_1_out), .clr(reset));
  RAM #(.addrWidth(16), .bus("separate")) ram_4 (
    .addr(RAM_ADDR), .din(RAM_DOUT[31:24]), .data(RAM_DIN[31:24]), .str(and_2_out), .sel(RAM_BE[3]),
    .clk(clk), .ld(and_1_out), .clr(reset));

  // Notes on the sheet:
  //   en: pull=up
endmodule

module Memory_BE_Registered (
  input  clk,
  input  reset,
  input  en,
  input  RAM_STB,
  input  RAM_WR,
  input  [3:0] RAM_BE,
  input  [15:0] RAM_ADDR,
  input  [31:0] RAM_DOUT,
  output RAM_ACK,
  output [31:0] RAM_DIN
);

  Register #(.width(1)) register_1 ();  // open: D, en, Q, clk, clr

  // Notes on the sheet:
  //   en: pull=up
endmodule
